// Logisim project CH6.circ as structural Verilog: 13 circuits, main circuit Latch
module Latch (
  input  in_1,
  input  in_2,
  output out_1,
  output out_2
);

  nand nand_1 (out_1, in_1, out_2);
  nand nand_2 (out_2, out_1, in_2);
endmodule

module Latch_w_sync_in (
  input  in_1,
  input  sync,
  input  in_2,
  output out_1,
  output out_2
);

  wire nand_1_out, nand_2_out;

  nand nand_1 (nand_1_out, in_1, sync);
  nand nand_2 (nand_2_out, sync, in_2);
  nand nand_3 (out_1, nand_1_out, out_2);
  nand nand_4 (out_2, out_1, nand_2_out);
endmodule

module D_type_Flip_Flop (
  input  in_1,
  input  sync,
  output out_1,
  output out_2
);

  wire nand_1_out, nand_2_out, nand_3_out;

  nand nand_1 (nand_1_out, in_1, sync);
  nand nand_2 (nand_2_out, sync, nand_3_out);
  nand nand_3 (nand_3_out, in_1, in_1);
  nand nand_4 (out_1, nand_1_out, out_2);
  nand nand_5 (out_2, out_1, nand_2_out);
endmodule

module _7400 (
  input  _1,
  input  Vcc,
  input  _2,
  input  _13,
  input  _12,
  input  _4,
  input  _5,
  input  _10,
  input  _9,
  input  GND,
  output _3,
  output _11,
  output _6,
  output _8
);

  nand nand_1 (_3, _2, _1);
  nand nand_2 (_6, _5, _4);
  nand nand_3 (_11, _13, _12);
  nand nand_4 (_8, _10, _9);
endmodule

module _7404 (
  input  _1,
  input  Vcc,
  input  _13,
  input  _3,
  input  _11,
  input  _5,
  input  _9,
  input  GND,
  output _2,
  output _12,
  output _4,
  output _10,
  output _6,
  output _8
);

  not not_1 (_2, _1);
  not not_2 (_4, _3);
  not not_3 (_6, _5);
  not not_4 (_12, _13);
  not not_5 (_10, _11);
  not not_6 (_8, _9);
endmodule

module False_Button (
  input  in_1,
  input  in_2,
  output out_3,
  output out_4
);
endmodule

module False_LED (
  input  in_1,
  output out_2
);


  assign out_2 = in_1;
endmodule

module Flip_Flop_Wiring (
);

  wire false_button_1_out_3, false_button_1_out_4, false_button_2_out_4, false_button_3_out_3,
       false_button_3_out_4, false_button_4_out_3, false_button_4_out_4, false_led_1_out_2, n7400_1__3,
       n7400_1__6, n7400_1__8, n7400_1__11, n7400_2__3, n7400_2__6, n7400_2__8, n7400_2__11, n7404_1__12,
       n7404_2__2, n7404_2__4, n7404_2__6, n7404_2__8, n7404_2__10, n7404_2__12, undriven, undriven_2,
       undriven_3, undriven_4, undriven_5, undriven_6, undriven_7, undriven_8, undriven_9, undriven_10,
       undriven_11, undriven_12, undriven_13, undriven_14, undriven_15, undriven_16, undriven_17,
       undriven_18, undriven_19, undriven_20, undriven_21, undriven_22, undriven_23, undriven_24,
       undriven_25, undriven_26;

  False_LED false_led_1 (.in_1(undriven), .out_2(false_led_1_out_2));
  False_LED false_led_2 (.in_1(undriven_2), .out_2(false_led_1_out_2));
  False_Button false_button_1 (
    .in_2(undriven_3), .out_3(false_button_1_out_3), .out_4(false_button_1_out_4));  // open: in_1
  False_Button false_button_2 (
    .in_2(undriven_4), .out_3(false_button_1_out_3), .out_4(false_button_2_out_4));  // open: in_1
  _7404 u_7404_1 (
    .GND(false_led_1_out_2), .Vcc(false_button_1_out_3), ._13(false_button_2_out_4), ._12(n7404_1__12));  // open: _1, _2, _3, _4, _5, _6, _11, _10, _9, _8
  _7400 u_7400_1 (
    ._1(undriven_4), ._2(undriven_3), ._3(n7400_1__3), ._4(n7400_1__3), ._5(n7400_1__8), ._6(n7400_1__6),
    .GND(false_led_1_out_2), .Vcc(false_button_1_out_3), ._13(n7404_1__12), ._12(false_button_1_out_4),
    ._11(n7400_1__11), ._10(n7400_1__11), ._9(n7400_1__6), ._8(n7400_1__8));
  Pull_Resistor pull_resistor_1 (.node(n7400_1__6));
  Pull_Resistor pull_resistor_2 (.node(n7400_1__8));
  False_LED false_led_3 ();  // open: in_1, out_2
  _7400 u_7400_2 (
    ._1(undriven_5), ._2(undriven_6), ._3(n7400_2__3), ._4(undriven_7), ._5(undriven_8), ._6(n7400_2__6),
    .GND(undriven_9), .Vcc(undriven_18), ._13(undriven_19), ._12(undriven_20), ._11(n7400_2__11),
    ._10(undriven_21), ._9(undriven_22), ._8(n7400_2__8));
  _7404 u_7404_2 (
    ._1(undriven_10), ._2(n7404_2__2), ._3(undriven_11), ._4(n7404_2__4), ._5(undriven_12), ._6(n7404_2__6),
    .GND(undriven_13), .Vcc(undriven_23), ._13(undriven_24), ._12(n7404_2__12), ._11(undriven_25),
    ._10(n7404_2__10), ._9(undriven_26), ._8(n7404_2__8));
  False_Button false_button_3 (
    .in_1(undriven_14), .in_2(undriven_15), .out_3(false_button_3_out_3), .out_4(false_button_3_out_4));
  False_Button false_button_4 (
    .in_1(undriven_16), .in_2(undriven_17), .out_3(false_button_4_out_3), .out_4(false_button_4_out_4));
  // also tied to GND on the sheet: false_led_1_out_2
  // also tied to VCC on the sheet: false_button_1_out_3
endmodule

// Instruction Register
module _16_bit_register (
  input  [15:0] Input,
  input  Clock,
  output [15:0] Output
);

  D_Flip_Flop d_ff_1 (.clk(Clock), .D(Input[0]), .Q(Output[0]));  // open: Qn, preset, en, reset
  D_Flip_Flop d_ff_2 (.clk(Clock), .D(Input[1]), .Q(Output[1]));  // open: Qn, preset, en, reset
  D_Flip_Flop d_ff_3 (.clk(Clock), .D(Input[2]), .Q(Output[2]));  // open: Qn, preset, en, reset
  D_Flip_Flop d_ff_4 (.clk(Clock), .D(Input[3]), .Q(Output[3]));  // open: Qn, preset, en, reset
  D_Flip_Flop d_ff_5 (.clk(Clock), .D(Input[4]), .Q(Output[4]));  // open: Qn, preset, en, reset
  D_Flip_Flop d_ff_6 (.clk(Clock), .D(Input[5]), .Q(Output[5]));  // open: Qn, preset, en, reset
  D_Flip_Flop d_ff_7 (.clk(Clock), .D(Input[6]), .Q(Output[6]));  // open: Qn, preset, en, reset
  D_Flip_Flop d_ff_8 (.clk(Clock), .D(Input[7]), .Q(Output[7]));  // open: Qn, preset, en, reset
  D_Flip_Flop d_ff_9 (.clk(Clock), .D(Input[8]), .Q(Output[8]));  // open: Qn, preset, en, reset
  D_Flip_Flop d_ff_10 (.clk(Clock), .D(Input[9]), .Q(Output[9]));  // open: Qn, preset, en, reset
  D_Flip_Flop d_ff_11 (.clk(Clock), .D(Input[10]), .Q(Output[10]));  // open: Qn, preset, en, reset
  D_Flip_Flop d_ff_12 (.clk(Clock), .D(Input[11]), .Q(Output[11]));  // open: Qn, preset, en, reset
  D_Flip_Flop d_ff_13 (.clk(Clock), .D(Input[12]), .Q(Output[12]));  // open: Qn, preset, en, reset
  D_Flip_Flop d_ff_14 (.clk(Clock), .D(Input[13]), .Q(Output[13]));  // open: Qn, preset, en, reset
  D_Flip_Flop d_ff_15 (.clk(Clock), .D(Input[14]), .Q(Output[14]));  // open: Qn, preset, en, reset
  D_Flip_Flop d_ff_16 (.clk(Clock), .D(Input[15]), .Q(Output[15]));  // open: Qn, preset, en, reset
endmodule

module _16_bit_8_word_register (
  input  [15:0] Data_In,
  input  [2:0] Select_In,
  input  Clock,
  output [15:0] Data_Out
);

  wire demultiplexer_1_out0, demultiplexer_1_out1, demultiplexer_1_out2, demultiplexer_1_out3,
       demultiplexer_1_out4, demultiplexer_1_out5, demultiplexer_1_out6, demultiplexer_1_out7;
  wire [15:0] n16_bit_register_1_output, n16_bit_register_2_output, n16_bit_register_3_output,
       n16_bit_register_4_output, n16_bit_register_5_output, n16_bit_register_6_output,
       n16_bit_register_7_output, n16_bit_register_8_output;

  Demultiplexer #(.select(3), .enable("false")) demultiplexer_1 (
    .out0(demultiplexer_1_out0), .out1(demultiplexer_1_out1), .out2(demultiplexer_1_out2),
    .out3(demultiplexer_1_out3), .out4(demultiplexer_1_out4), .out5(demultiplexer_1_out5),
    .out6(demultiplexer_1_out6), .out7(demultiplexer_1_out7), .in(Clock), .sel(Select_In));
  // Probe on n16_bit_register_1_output
  _16_bit_register u_16_bit_register_1 (
    .Input(Data_In), .Output(n16_bit_register_1_output), .Clock(demultiplexer_1_out0));
  _16_bit_register u_16_bit_register_2 (
    .Input(Data_In), .Output(n16_bit_register_2_output), .Clock(demultiplexer_1_out1));
  // Probe on n16_bit_register_2_output
  // Probe on n16_bit_register_3_output
  _16_bit_register u_16_bit_register_3 (
    .Input(Data_In), .Output(n16_bit_register_3_output), .Clock(demultiplexer_1_out2));
  // Probe on n16_bit_register_4_output
  _16_bit_register u_16_bit_register_4 (
    .Input(Data_In), .Output(n16_bit_register_4_output), .Clock(demultiplexer_1_out3));
  // Probe on n16_bit_register_5_output
  _16_bit_register u_16_bit_register_5 (
    .Input(Data_In), .Output(n16_bit_register_5_output), .Clock(demultiplexer_1_out4));
  _16_bit_register u_16_bit_register_6 (
    .Input(Data_In), .Output(n16_bit_register_6_output), .Clock(demultiplexer_1_out5));
  // Probe on n16_bit_register_6_output
  _16_bit_register u_16_bit_register_7 (
    .Input(Data_In), .Output(n16_bit_register_7_output), .Clock(demultiplexer_1_out6));
  // Probe on n16_bit_register_7_output
  // Probe on n16_bit_register_8_output
  _16_bit_register u_16_bit_register_8 (
    .Input(Data_In), .Output(n16_bit_register_8_output), .Clock(demultiplexer_1_out7));
  Multiplexer #(.select(3), .width(16), .disabled(0), .enable("false")) multiplexer_1 (
    .in0(n16_bit_register_1_output), .in1(n16_bit_register_2_output), .in2(n16_bit_register_3_output),
    .in3(n16_bit_register_4_output), .in4(n16_bit_register_5_output), .in5(n16_bit_register_6_output),
    .in6(n16_bit_register_7_output), .in7(n16_bit_register_8_output), .out(Data_Out), .sel(Select_In));
endmodule

module D_FlipFlop (
  input  Clock,
  input  In,
  output Out,
  output Out_inverted
);

  D_Flip_Flop d_ff_1 (.clk(Clock), .D(In), .Q(Out), .Qn(Out_inverted));  // open: preset, en, reset
endmodule

module octal_counter (
  input  Clock_in,
  output [2:0] Out
);

  wire d_ff_1_q, d_ff_2_q;

  D_Flip_Flop d_ff_1 (.clk(Clock_in), .D(Out[0]), .Q(d_ff_1_q), .Qn(Out[0]));  // open: preset, en, reset
  D_Flip_Flop d_ff_2 (.clk(d_ff_1_q), .D(Out[1]), .Q(d_ff_2_q), .Qn(Out[1]));  // open: preset, en, reset
  D_Flip_Flop d_ff_3 (.clk(d_ff_2_q), .D(Out[2]), .Qn(Out[2]));  // open: Q, preset, en, reset
endmodule

module hex_counter (
  input  Clock_in,
  output [3:0] Out
);

  wire d_ff_1_q, d_ff_2_q, d_ff_3_q;

  D_Flip_Flop d_ff_1 (.clk(Clock_in), .D(Out[0]), .Q(d_ff_1_q), .Qn(Out[0]));  // open: preset, en, reset
  D_Flip_Flop d_ff_2 (.clk(d_ff_1_q), .D(Out[1]), .Q(d_ff_2_q), .Qn(Out[1]));  // open: preset, en, reset
  D_Flip_Flop d_ff_3 (.clk(d_ff_2_q), .D(Out[2]), .Q(d_ff_3_q), .Qn(Out[2]));  // open: preset, en, reset
  D_Flip_Flop d_ff_4 (.clk(d_ff_3_q), .D(Out[3]), .Qn(Out[3]));  // open: Q, preset, en, reset
endmodule
