// Logisim project Ch7.circ as structural Verilog
module processor (
);

  wire AluInAClk, AluInBClk, AluOutClk, CarryInClk, Decode, InsRegClk, MemClk, MemInClk, MemOutClk,
       MemSelClk, n2_x_7_seg_1_out_2, n2_x_7_seg_1_out_3, n2_x_7_seg_1_out_4, n2_x_7_seg_1_out_5,
       n2_x_7_seg_1_out_6, n2_x_7_seg_1_out_7, n2_x_7_seg_1_out_8, n2_x_7_seg_1_out_9, n2_x_7_seg_1_out_10,
       n2_x_7_seg_1_out_11, n2_x_7_seg_1_out_12, n2_x_7_seg_1_out_13, n2_x_7_seg_1_out_14,
       n2_x_7_seg_1_out_15, n2_x_7_seg_1_out_16, n2_x_7_seg_1_out_17, n3_x_7_seg_1_out_2, n3_x_7_seg_1_out_3,
       n3_x_7_seg_1_out_4, n3_x_7_seg_1_out_5, n3_x_7_seg_1_out_6, n3_x_7_seg_1_out_7, n3_x_7_seg_1_out_8,
       n3_x_7_seg_1_out_9, n3_x_7_seg_1_out_10, n3_x_7_seg_1_out_11, n3_x_7_seg_1_out_12,
       n3_x_7_seg_1_out_13, n3_x_7_seg_1_out_14, n3_x_7_seg_1_out_15, n3_x_7_seg_1_out_16,
       n3_x_7_seg_1_out_17, n3_x_7_seg_1_out_18, n3_x_7_seg_1_out_19, n3_x_7_seg_1_out_20,
       n3_x_7_seg_1_out_21, n3_x_7_seg_1_out_22, n3_x_7_seg_1_out_23, n3_x_7_seg_1_out_24,
       n3_x_7_seg_1_out_25, n6_x_7_seg_1_out_2, n6_x_7_seg_1_out_3, n6_x_7_seg_1_out_4, n6_x_7_seg_1_out_5,
       n6_x_7_seg_1_out_6, n6_x_7_seg_1_out_7, n6_x_7_seg_1_out_8, n6_x_7_seg_1_out_9, n6_x_7_seg_1_out_10,
       n6_x_7_seg_1_out_11, n6_x_7_seg_1_out_12, n6_x_7_seg_1_out_13, n6_x_7_seg_1_out_14,
       n6_x_7_seg_1_out_15, n6_x_7_seg_1_out_16, n6_x_7_seg_1_out_17, n6_x_7_seg_1_out_18,
       n6_x_7_seg_1_out_19, n6_x_7_seg_1_out_20, n6_x_7_seg_1_out_21, n6_x_7_seg_1_out_22,
       n6_x_7_seg_1_out_23, n6_x_7_seg_1_out_24, n6_x_7_seg_1_out_25, n6_x_7_seg_1_out_26,
       n6_x_7_seg_1_out_27, n6_x_7_seg_1_out_28, n6_x_7_seg_1_out_29, n6_x_7_seg_1_out_30,
       n6_x_7_seg_1_out_31, n6_x_7_seg_1_out_32, n6_x_7_seg_1_out_33, n6_x_7_seg_1_out_34,
       n6_x_7_seg_1_out_35, n6_x_7_seg_1_out_36, n6_x_7_seg_1_out_37, n6_x_7_seg_1_out_38,
       n6_x_7_seg_1_out_39, n6_x_7_seg_1_out_40, n6_x_7_seg_1_out_41, n6_x_7_seg_1_out_42,
       n6_x_7_seg_1_out_43, n6_x_7_seg_1_out_44, n6_x_7_seg_1_out_45, n6_x_7_seg_1_out_46,
       n6_x_7_seg_1_out_47, n6_x_7_seg_1_out_48, n6_x_7_seg_1_out_49, RegClk, RegInClk, Registers_p10,
       RegOutClk, RegSelClk;
  wire [1:0] InsRegSel, RegInpSel;
  wire [2:0] multiplexer_2_out, n16_bit_alu_2_1_out_6, register_3_q, register_6_q, register_7_q,
       register_11_q, register_15_q;
  wire [3:0] register_8_q;
  wire [4:0] register_2_q;
  wire [7:0] register_9_q;
  wire [15:0] carry_in_1_out, control_logic_1_microstep, memory_1_data_out, multiplexer_1_out,
       n16_bit_alu_2_1_result, register_1_q, register_4_q, register_5_q, register_10_q, register_13_q,
       register_16_q, register_17_q, register_18_q, register_19_q, Registers_p2, Registers_p3, Registers_p4,
       Registers_p5, Registers_p8, Registers_p9, Registers_p11, Registers_p12, Registers_p13;

  Control_Logic control_logic_1 (
    .Decode(Decode), .InsRegClk(InsRegClk), .AluInAClk(AluInAClk), .AluInBClk(AluInBClk),
    .AluOutClk(AluOutClk), .RegClk(RegClk), .RegOutClk(RegOutClk), .MemClk(MemClk), .MemSelClk(MemSelClk),
    .MemInClk(MemInClk), .MemOutClk(MemOutClk), .CarryInClk(CarryInClk), .RegInpSel(RegInpSel),
    .InsRegSel(InsRegSel), .OpCode(register_2_q), .MicroStep(control_logic_1_microstep[3:0]),
    .RegSelClk(RegSelClk), .RegInClk(RegInClk), .N_Z_P_2(register_1_q[4:2]), .N_Z_P(register_11_q),
    .Reset(Registers_p10));
  Register #(.width(16), .trigger("high")) register_1 (
    .D(register_19_q), .Q(register_1_q), .clk(InsRegClk));  // open: en, clr
  Register #(.width(5), .trigger("high")) register_2 (
    .D(register_1_q[15:11]), .Q(register_2_q), .clk(Decode));  // open: en, clr
  Register #(.width(3), .trigger("high")) register_3 (
    .D(register_1_q[10:8]), .Q(register_3_q), .clk(Decode));  // open: en, clr
  Register #(.width(16), .trigger("high")) register_4 (
    .D(register_18_q), .Q(register_4_q), .clk(AluInAClk));  // open: en, clr
  Register #(.width(16), .trigger("high")) register_5 (
    .D(register_18_q), .Q(register_5_q), .clk(AluInBClk));  // open: en, clr
  Register #(.width(3), .trigger("high")) register_6 (
    .D(register_1_q[7:5]), .Q(register_6_q), .clk(Decode));  // open: en, clr
  Register #(.width(3), .trigger("high")) register_7 (
    .D(register_1_q[4:2]), .Q(register_7_q), .clk(Decode));  // open: en, clr
  Register #(.width(4), .trigger("high")) register_8 (
    .D(register_2_q[3:0]), .Q(register_8_q), .clk(1'b1));  // open: en, clr
  Register #(.trigger("high")) register_9 (.D(register_1_q[7:0]), .Q(register_9_q), .clk(Decode));  // open: en, clr
  Register #(.width(16), .trigger("high")) register_10 (
    .D(n16_bit_alu_2_1_result), .Q(register_10_q), .clk(AluOutClk));  // open: en, clr
  _16_bit_alu_2 u_16_bit_alu_2_1 (
    .A(register_4_q), .B(register_5_q), .Result(n16_bit_alu_2_1_result), .in_1(register_8_q),
    .out_6(n16_bit_alu_2_1_out_6));  // open: CarryOut_Overflow
  Register #(.width(3), .trigger("high")) register_11 (
    .D(n16_bit_alu_2_1_out_6), .Q(register_11_q), .clk(register_2_q[4]));  // open: en, clr
  Multiplexer #(.select(2), .width(16), .enable("false")) multiplexer_1 (
    .in0({{8{1'b0}}, register_9_q}), .in1(register_19_q), .in2(register_10_q), .in3(carry_in_1_out),
    .out(multiplexer_1_out), .sel(RegInpSel));
  // Probe on RegInpSel
  Carry_In carry_in_1 (.IN(register_18_q), .Out(carry_in_1_out), .Carry_In(CarryInClk));
  Register #(.width(16), .trigger("high")) register_12 (.D(carry_in_1_out), .clk(1'b1));  // open: en, Q, clr
  Multiplexer #(.select(2), .width(3), .enable("false")) multiplexer_2 (
    .in0(3'b000), .in1(register_3_q), .in2(register_6_q), .in3(register_7_q), .out(multiplexer_2_out),
    .sel(InsRegSel));
  // Probe on multiplexer_2_out
  Register #(.width(16), .trigger("high")) register_13 (
    .D(multiplexer_1_out), .Q(register_13_q), .clk(RegInClk));  // open: en, clr
  Register #(.width(16), .trigger("high")) register_14 (.D(register_18_q), .clk(1'b1));  // open: en, Q, clr
  Register #(.width(3), .trigger("high")) register_15 (
    .D(multiplexer_2_out), .Q(register_15_q), .clk(RegSelClk));  // open: en, clr
  // _16_bit_8_word_register Registers: pin names not known; wires that end beside it: register_13_q, Registers_p2, Registers_p3, Registers_p4, Registers_p5, register_15_q, RegClk, Registers_p8, Registers_p9, Registers_p10, Registers_p11, Registers_p12, Registers_p13
  Register #(.width(16), .trigger("high")) register_16 (
    .D(register_18_q), .Q(register_16_q), .clk(MemSelClk));  // open: en, clr
  Memory memory_1 (
    .Data_In(register_17_q), .Data_Out(memory_1_data_out), .Memory_Address(register_16_q), .Clock(MemClk));  // open: CLEAR
  Register #(.width(16), .trigger("high")) register_17 (
    .D(register_18_q), .Q(register_17_q), .clk(MemInClk));  // open: en, clr
  Button button_1 (.out(Registers_p10));
  Register #(.width(16), .trigger("high")) register_18 (
    .D(Registers_p12), .Q(register_18_q), .clk(RegOutClk));  // open: en, clr
  Register #(.width(16), .trigger("high")) register_19 (
    .D(memory_1_data_out), .Q(register_19_q), .clk(MemOutClk));  // open: en, clr
  _6_X_7_seg u_6_x_7_seg_1 (
    .in_1(Registers_p11), .out_2(n6_x_7_seg_1_out_2), .out_3(n6_x_7_seg_1_out_3), .out_4(n6_x_7_seg_1_out_4),
    .out_5(n6_x_7_seg_1_out_5), .out_26(n6_x_7_seg_1_out_26), .out_27(n6_x_7_seg_1_out_27),
    .out_28(n6_x_7_seg_1_out_28), .out_29(n6_x_7_seg_1_out_29), .out_6(n6_x_7_seg_1_out_6),
    .out_7(n6_x_7_seg_1_out_7), .out_8(n6_x_7_seg_1_out_8), .out_9(n6_x_7_seg_1_out_9),
    .out_30(n6_x_7_seg_1_out_30), .out_31(n6_x_7_seg_1_out_31), .out_32(n6_x_7_seg_1_out_32),
    .out_33(n6_x_7_seg_1_out_33), .out_10(n6_x_7_seg_1_out_10), .out_11(n6_x_7_seg_1_out_11),
    .out_12(n6_x_7_seg_1_out_12), .out_13(n6_x_7_seg_1_out_13), .out_34(n6_x_7_seg_1_out_34),
    .out_35(n6_x_7_seg_1_out_35), .out_36(n6_x_7_seg_1_out_36), .out_37(n6_x_7_seg_1_out_37),
    .out_14(n6_x_7_seg_1_out_14), .out_15(n6_x_7_seg_1_out_15), .out_16(n6_x_7_seg_1_out_16),
    .out_17(n6_x_7_seg_1_out_17), .out_38(n6_x_7_seg_1_out_38), .out_39(n6_x_7_seg_1_out_39),
    .out_40(n6_x_7_seg_1_out_40), .out_41(n6_x_7_seg_1_out_41), .out_18(n6_x_7_seg_1_out_18),
    .out_19(n6_x_7_seg_1_out_19), .out_20(n6_x_7_seg_1_out_20), .out_21(n6_x_7_seg_1_out_21),
    .out_42(n6_x_7_seg_1_out_42), .out_43(n6_x_7_seg_1_out_43), .out_44(n6_x_7_seg_1_out_44),
    .out_45(n6_x_7_seg_1_out_45), .out_22(n6_x_7_seg_1_out_22), .out_23(n6_x_7_seg_1_out_23),
    .out_24(n6_x_7_seg_1_out_24), .out_25(n6_x_7_seg_1_out_25), .out_46(n6_x_7_seg_1_out_46),
    .out_47(n6_x_7_seg_1_out_47), .out_48(n6_x_7_seg_1_out_48), .out_49(n6_x_7_seg_1_out_49));
  _7_Segment_Display u_7_segment_display_1 (
    .g(n6_x_7_seg_1_out_2), .f(n6_x_7_seg_1_out_3), .a(n6_x_7_seg_1_out_4), .b(n6_x_7_seg_1_out_5),
    .e(n6_x_7_seg_1_out_26), .d(n6_x_7_seg_1_out_27), .c(n6_x_7_seg_1_out_28), .dp(n6_x_7_seg_1_out_29));
  _7_Segment_Display u_7_segment_display_2 (
    .g(n3_x_7_seg_1_out_2), .f(n3_x_7_seg_1_out_3), .a(n3_x_7_seg_1_out_4), .b(n3_x_7_seg_1_out_5),
    .e(n3_x_7_seg_1_out_14), .d(n3_x_7_seg_1_out_15), .c(n3_x_7_seg_1_out_16), .dp(n3_x_7_seg_1_out_17));
  _7_Segment_Display u_7_segment_display_3 (
    .g(n3_x_7_seg_1_out_6), .f(n3_x_7_seg_1_out_7), .a(n3_x_7_seg_1_out_8), .b(n3_x_7_seg_1_out_9),
    .e(n3_x_7_seg_1_out_18), .d(n3_x_7_seg_1_out_19), .c(n3_x_7_seg_1_out_20), .dp(n3_x_7_seg_1_out_21));
  _3_X_7_seg u_3_x_7_seg_1 (
    .out_2(n3_x_7_seg_1_out_2), .out_3(n3_x_7_seg_1_out_3), .out_4(n3_x_7_seg_1_out_4),
    .out_5(n3_x_7_seg_1_out_5), .out_6(n3_x_7_seg_1_out_6), .in_1(Registers_p13), .out_7(n3_x_7_seg_1_out_7),
    .out_8(n3_x_7_seg_1_out_8), .out_9(n3_x_7_seg_1_out_9), .out_10(n3_x_7_seg_1_out_10),
    .out_11(n3_x_7_seg_1_out_11), .out_12(n3_x_7_seg_1_out_12), .out_13(n3_x_7_seg_1_out_13),
    .out_14(n3_x_7_seg_1_out_14), .out_15(n3_x_7_seg_1_out_15), .out_16(n3_x_7_seg_1_out_16),
    .out_17(n3_x_7_seg_1_out_17), .out_18(n3_x_7_seg_1_out_18), .out_19(n3_x_7_seg_1_out_19),
    .out_20(n3_x_7_seg_1_out_20), .out_21(n3_x_7_seg_1_out_21), .out_22(n3_x_7_seg_1_out_22),
    .out_23(n3_x_7_seg_1_out_23), .out_24(n3_x_7_seg_1_out_24), .out_25(n3_x_7_seg_1_out_25));
  Register #(.width(16), .trigger("high")) register_20 (.D(Registers_p13), .clk(1'b1));  // open: en, Q, clr
  Register #(.width(16), .trigger("high")) register_21 (.D(Registers_p11), .clk(1'b1));  // open: en, Q, clr
  Register #(.width(16), .trigger("high")) register_22 (.D(Registers_p9), .clk(1'b1));  // open: en, Q, clr
  Register #(.width(16), .trigger("high")) register_23 (.D(Registers_p8), .clk(1'b1));  // open: en, Q, clr
  _7_Segment_Display u_7_segment_display_4 (
    .g(n6_x_7_seg_1_out_10), .f(n6_x_7_seg_1_out_11), .a(n6_x_7_seg_1_out_12), .b(n6_x_7_seg_1_out_13),
    .e(n6_x_7_seg_1_out_34), .d(n6_x_7_seg_1_out_35), .c(n6_x_7_seg_1_out_36), .dp(n6_x_7_seg_1_out_37));
  _7_Segment_Display u_7_segment_display_5 (
    .g(n6_x_7_seg_1_out_6), .f(n6_x_7_seg_1_out_7), .a(n6_x_7_seg_1_out_8), .b(n6_x_7_seg_1_out_9),
    .e(n6_x_7_seg_1_out_30), .d(n6_x_7_seg_1_out_31), .c(n6_x_7_seg_1_out_32), .dp(n6_x_7_seg_1_out_33));
  _7_Segment_Display u_7_segment_display_6 (
    .g(n3_x_7_seg_1_out_10), .f(n3_x_7_seg_1_out_11), .a(n3_x_7_seg_1_out_12), .b(n3_x_7_seg_1_out_13),
    .e(n3_x_7_seg_1_out_22), .d(n3_x_7_seg_1_out_23), .c(n3_x_7_seg_1_out_24), .dp(n3_x_7_seg_1_out_25));
  Register #(.width(16), .trigger("high")) register_24 (.D(Registers_p5), .clk(1'b1));  // open: en, Q, clr
  Register #(.width(16), .trigger("high")) register_25 (.D(Registers_p4), .clk(1'b1));  // open: en, Q, clr
  Register #(.width(16), .trigger("high")) register_26 (.D(Registers_p3), .clk(1'b1));  // open: en, Q, clr
  Register #(.width(16), .trigger("high")) register_27 (.D(Registers_p2), .clk(1'b1));  // open: en, Q, clr
  _7_Segment_Display u_7_segment_display_7 (
    .g(n6_x_7_seg_1_out_18), .f(n6_x_7_seg_1_out_19), .a(n6_x_7_seg_1_out_20), .b(n6_x_7_seg_1_out_21),
    .e(n6_x_7_seg_1_out_42), .d(n6_x_7_seg_1_out_43), .c(n6_x_7_seg_1_out_44), .dp(n6_x_7_seg_1_out_45));
  _7_Segment_Display u_7_segment_display_8 (
    .g(n6_x_7_seg_1_out_14), .f(n6_x_7_seg_1_out_15), .a(n6_x_7_seg_1_out_16), .b(n6_x_7_seg_1_out_17),
    .e(n6_x_7_seg_1_out_38), .d(n6_x_7_seg_1_out_39), .c(n6_x_7_seg_1_out_40), .dp(n6_x_7_seg_1_out_41));
  _7_Segment_Display u_7_segment_display_9 (
    .g(n2_x_7_seg_1_out_6), .f(n2_x_7_seg_1_out_7), .a(n2_x_7_seg_1_out_8), .b(n2_x_7_seg_1_out_9),
    .e(n2_x_7_seg_1_out_14), .d(n2_x_7_seg_1_out_15), .c(n2_x_7_seg_1_out_16), .dp(n2_x_7_seg_1_out_17));
  _7_Segment_Display u_7_segment_display_10 (
    .g(n2_x_7_seg_1_out_2), .f(n2_x_7_seg_1_out_3), .a(n2_x_7_seg_1_out_4), .b(n2_x_7_seg_1_out_5),
    .e(n2_x_7_seg_1_out_10), .d(n2_x_7_seg_1_out_11), .c(n2_x_7_seg_1_out_12), .dp(n2_x_7_seg_1_out_13));
  _7_Segment_Display u_7_segment_display_11 (
    .g(n6_x_7_seg_1_out_22), .f(n6_x_7_seg_1_out_23), .a(n6_x_7_seg_1_out_24), .b(n6_x_7_seg_1_out_25),
    .e(n6_x_7_seg_1_out_46), .d(n6_x_7_seg_1_out_47), .c(n6_x_7_seg_1_out_48), .dp(n6_x_7_seg_1_out_49));
  _2_X_7_seg u_2_x_7_seg_1 (
    .out_2(n2_x_7_seg_1_out_2), .out_3(n2_x_7_seg_1_out_3), .out_4(n2_x_7_seg_1_out_4),
    .out_5(n2_x_7_seg_1_out_5), .out_6(n2_x_7_seg_1_out_6), .out_7(n2_x_7_seg_1_out_7),
    .out_8(n2_x_7_seg_1_out_8), .out_9(n2_x_7_seg_1_out_9), .in_1(control_logic_1_microstep),
    .out_10(n2_x_7_seg_1_out_10), .out_11(n2_x_7_seg_1_out_11), .out_12(n2_x_7_seg_1_out_12),
    .out_13(n2_x_7_seg_1_out_13), .out_14(n2_x_7_seg_1_out_14), .out_15(n2_x_7_seg_1_out_15),
    .out_16(n2_x_7_seg_1_out_16), .out_17(n2_x_7_seg_1_out_17));

  // Notes on the sheet:
  //   Program Counter
  //   R4
  //   R5
  //   R6
  //   R7
endmodule

module Control_Logic (
  input  [4:0] OpCode,
  input  Reset,
  input  [2:0] N_Z_P,
  input  [2:0] N_Z_P_2,
  output [3:0] MicroStep,
  output [1:0] InsRegSel,
  output RegSelClk,
  output RegOutClk,
  output MemOutClk,
  output MemSelClk,
  output CarryInClk,
  output [1:0] RegInpSel,
  output RegInClk,
  output AluInAClk,
  output AluInBClk,
  output AluOutClk,
  output MemInClk,
  output MemClk,
  output RegClk,
  output InsRegClk,
  output Decode
);

  wire and_1_out, and_2_out, and_3_out, and_4_out, and_5_out, and_6_out, clock_1_out, nor_1_out, not_1_out,
       not_2_out, not_3_out, or_1_out, or_2_out, or_3_out, or_4_out;
  wire [3:0] demultiplexer_1_out0;
  wire [9:0] demultiplexer_1_out6, demultiplexer_2_out0, demultiplexer_2_out1, demultiplexer_3_out0,
       demultiplexer_3_out1, demultiplexer_3_out2, demultiplexer_3_out3;

  not not_1 (not_1_out, OpCode[4]);
  and and_1 (and_1_out, not_1_out, OpCode[3], OpCode[2]);
  Pull_Resistor pull_resistor_1 (.node(and_1_out));
  not not_2 (not_2_out, and_1_out);
  Clock clock_1 (.out(clock_1_out));
  and and_2 (and_2_out, N_Z_P[2], N_Z_P_2[2]);
  Counter_part #(.width(4), .max('hf)) counter_1 (
    .Q(MicroStep), .clk(and_3_out), .clr(or_1_out));  // open: load, D, count, carry
  and and_3 (and_3_out, clock_1_out, not_2_out);
  or or_1 (or_1_out, Reset, and_4_out, demultiplexer_3_out3[7], demultiplexer_3_out2[6], demultiplexer_3_out1[4], demultiplexer_3_out0[6], demultiplexer_2_out0[9]);
  and and_4 (and_4_out, nor_1_out, demultiplexer_3_out3[0]);
  nor nor_1 (nor_1_out, and_2_out, and_5_out, and_6_out);
  and and_5 (and_5_out, N_Z_P[1], N_Z_P_2[1]);
  and and_6 (and_6_out, N_Z_P[0], N_Z_P_2[0]);
  Demultiplexer #(.select(4), .enable("false")) demultiplexer_1 (
    .out0(demultiplexer_1_out0[0]), .out1(demultiplexer_1_out0[1]), .out2(CarryInClk),
    .out3(demultiplexer_1_out0[3]), .out4(InsRegClk), .out5(Decode), .out6(demultiplexer_1_out6[0]),
    .out7(demultiplexer_1_out6[1]), .out8(demultiplexer_1_out6[2]), .out9(demultiplexer_1_out6[3]),
    .out10(demultiplexer_1_out6[4]), .out11(demultiplexer_1_out6[5]), .out12(demultiplexer_1_out6[6]),
    .out13(demultiplexer_1_out6[7]), .out14(demultiplexer_1_out6[8]), .out15(demultiplexer_1_out6[9]),
    .in(1'b1), .sel(MicroStep));
  Demultiplexer #(.width(10), .disabled(0), .enable("false")) demultiplexer_2 (
    .out0({demultiplexer_2_out0[9:7], AluOutClk, AluInBClk, demultiplexer_2_out0[4:3], AluInAClk, demultiplexer_2_out0[1:0]}),
    .out1(demultiplexer_2_out1), .in(demultiplexer_1_out6), .sel(not_3_out));
  not not_3 (not_3_out, OpCode[4]);
  Demultiplexer #(.select(2), .width(10), .enable("false")) demultiplexer_3 (
    .out0(demultiplexer_3_out0), .out1(demultiplexer_3_out1),
    .out2({demultiplexer_3_out2[9:4], MemClk, demultiplexer_3_out2[2:0]}), .out3(demultiplexer_3_out3),
    .in(demultiplexer_2_out1), .sel(OpCode[1:0]));
  or or_2 (or_2_out, demultiplexer_2_out0[0], demultiplexer_3_out0[2], demultiplexer_3_out1[0], demultiplexer_3_out2[2], demultiplexer_3_out3[1]);
  or or_3 (or_3_out, demultiplexer_2_out0[3], demultiplexer_3_out0[0], demultiplexer_3_out2[0], demultiplexer_3_out3[3]);
  or or_4 (or_4_out, CarryInClk, demultiplexer_3_out3[4]);
  Selector selector_1 (
    ._00(demultiplexer_1_out0[0]), ._01(or_2_out), ._10(or_3_out), ._11(AluOutClk), .X_(InsRegSel),
    .out_6(RegSelClk));
  or or_5 (RegOutClk, demultiplexer_1_out0[1], demultiplexer_2_out0[1], demultiplexer_2_out0[4], demultiplexer_3_out0[1], demultiplexer_3_out2[1], MemClk, demultiplexer_3_out3[2]);
  or or_6 (MemOutClk, CarryInClk, demultiplexer_3_out0[1]);
  or or_7 (MemSelClk, CarryInClk, demultiplexer_3_out0[1], demultiplexer_3_out2[1]);
  Selector selector_2 (
    ._00(demultiplexer_3_out1[1]), ._01(demultiplexer_3_out0[3]), ._10(demultiplexer_2_out0[7]),
    ._11(or_4_out), .X_(RegInpSel), .out_6(RegInClk));
  or or_8 (RegClk, demultiplexer_3_out3[5], demultiplexer_3_out1[2], demultiplexer_3_out0[4], demultiplexer_2_out0[8], demultiplexer_1_out0[3]);

  assign MemInClk = MemClk;

  // Notes on the sheet:
  //   N_Z_P: pull=down
  //   AluInAClk: pull=down
  //   N_Z_P_2: pull=down
  //   AluInBClk: pull=down
  //   RegSelClk: pull=down
  //   CarryInClk: pull=down
  //   RegClk: pull=down
  //   MemClk: pull=down
  //   AluOutClk: pull=down
  //   MemOutClk: pull=down
  //   RegOutClk: pull=down
  //   MemInClk: pull=down
  //   MemSelClk: pull=down
  //   Decode: pull=down
  //   InsRegClk: pull=down
  //   RegInClk: pull=down
endmodule

// 3
module _3_bit_register (
  input  Clock,
  input  [2:0] Input,
  input  Clock_2,
  output [2:0] Output
);

  D_Flip_Flop d_ff_1 (.clk(Clock), .D(Input[0]), .Q(Output[0]));  // open: Qn, preset, en, reset
  D_Flip_Flop d_ff_2 (.clk(Clock), .D(Input[1]), .Q(Output[1]));  // open: Qn, preset, en, reset
  D_Flip_Flop d_ff_3 (.clk(Clock), .D(Input[2]), .Q(Output[2]));  // open: Qn, preset, en, reset

  assign Clock_2 = Clock;
endmodule

// 5
module _5_bit_register (
  input  Clock,
  input  [4:0] Input,
  input  Clock_2,
  output [4:0] Output
);

  D_Flip_Flop d_ff_1 (.clk(Clock), .D(Input[0]), .Q(Output[0]));  // open: Qn, preset, en, reset
  D_Flip_Flop d_ff_2 (.clk(Clock), .D(Input[1]), .Q(Output[1]));  // open: Qn, preset, en, reset
  D_Flip_Flop d_ff_3 (.clk(Clock), .D(Input[2]), .Q(Output[2]));  // open: Qn, preset, en, reset
  D_Flip_Flop d_ff_4 (.clk(Clock), .D(Input[3]), .Q(Output[3]));  // open: Qn, preset, en, reset
  D_Flip_Flop d_ff_5 (.clk(Clock), .D(Input[4]), .Q(Output[4]));  // open: Qn, preset, en, reset

  assign Clock_2 = Clock;

  // Notes on the sheet:
  //   Input: pull=down
endmodule

// 8
module _8_bit_register (
  input  Clock,
  input  [7:0] Input,
  input  Clock_2,
  output [7:0] Output
);

  D_Flip_Flop d_ff_1 (.clk(Clock), .D(Input[0]), .Q(Output[0]));  // open: Qn, preset, en, reset
  D_Flip_Flop d_ff_2 (.clk(Clock), .D(Input[1]), .Q(Output[1]));  // open: Qn, preset, en, reset
  D_Flip_Flop d_ff_3 (.clk(Clock), .D(Input[2]), .Q(Output[2]));  // open: Qn, preset, en, reset
  D_Flip_Flop d_ff_4 (.clk(Clock), .D(Input[3]), .Q(Output[3]));  // open: Qn, preset, en, reset
  D_Flip_Flop d_ff_5 (.clk(Clock), .D(Input[4]), .Q(Output[4]));  // open: Qn, preset, en, reset
  D_Flip_Flop d_ff_6 (.clk(Clock), .D(Input[5]), .Q(Output[5]));  // open: Qn, preset, en, reset
  D_Flip_Flop d_ff_7 (.clk(Clock), .D(Input[6]), .Q(Output[6]));  // open: Qn, preset, en, reset
  D_Flip_Flop d_ff_8 (.clk(Clock), .D(Input[7]), .Q(Output[7]));  // open: Qn, preset, en, reset

  assign Clock_2 = Clock;
endmodule

// 16
module _16_bit_register (
  input  Clock,
  input  [15:0] Input,
  input  Clock_2,
  output [15:0] Output
);

  D_Flip_Flop d_ff_1 (.clk(Clock), .D(Input[14]), .Q(Output[14]));  // open: Qn, preset, en, reset
  D_Flip_Flop d_ff_2 (.clk(Clock), .D(Input[6]), .Q(Output[6]));  // open: Qn, preset, en, reset
  D_Flip_Flop d_ff_3 (.clk(Clock), .D(Input[8]), .Q(Output[8]));  // open: Qn, preset, en, reset
  D_Flip_Flop d_ff_4 (.clk(Clock), .D(Input[10]), .Q(Output[10]));  // open: Qn, preset, en, reset
  D_Flip_Flop d_ff_5 (.clk(Clock), .D(Input[12]), .Q(Output[12]));  // open: Qn, preset, en, reset
  D_Flip_Flop d_ff_6 (.clk(Clock), .D(Input[13]), .Q(Output[13]));  // open: Qn, preset, en, reset
  D_Flip_Flop d_ff_7 (.clk(Clock), .D(Input[15]), .Q(Output[15]));  // open: Qn, preset, en, reset
  D_Flip_Flop d_ff_8 (.clk(Clock), .D(Input[0]), .Q(Output[0]));  // open: Qn, preset, en, reset
  D_Flip_Flop d_ff_9 (.clk(Clock), .D(Input[2]), .Q(Output[2]));  // open: Qn, preset, en, reset
  D_Flip_Flop d_ff_10 (.clk(Clock), .D(Input[4]), .Q(Output[4]));  // open: Qn, preset, en, reset
  D_Flip_Flop d_ff_11 (.clk(Clock), .D(Input[5]), .Q(Output[5]));  // open: Qn, preset, en, reset
  D_Flip_Flop d_ff_12 (.clk(Clock), .D(Input[7]), .Q(Output[7]));  // open: Qn, preset, en, reset
  D_Flip_Flop d_ff_13 (.clk(Clock), .D(Input[9]), .Q(Output[9]));  // open: Qn, preset, en, reset
  D_Flip_Flop d_ff_14 (.clk(Clock), .D(Input[11]), .Q(Output[11]));  // open: Qn, preset, en, reset
  D_Flip_Flop d_ff_15 (.clk(Clock), .D(Input[1]), .Q(Output[1]));  // open: Qn, preset, en, reset
  D_Flip_Flop d_ff_16 (.clk(Clock), .D(Input[3]), .Q(Output[3]));  // open: Qn, preset, en, reset

  assign Clock_2 = Clock;
endmodule

module Instruction_Register (
  input  Decode,
  input  [15:0] In,
  input  Clock,
  output [15:0] Out
);

  Register #(.width(16), .trigger("high")) register_1 (.D(In), .clk(Clock));  // open: en, Q, clr

  assign Out = 16'h994c;
endmodule

module Carry_In (
  input  Carry_In,
  input  [15:0] IN,
  output [15:0] Out
);

  Adder #(.width(16)) adder_1 (.a(IN), .b({16{1'b0}}), .out(Out), .cin(Carry_In));  // open: cout

  // Notes on the sheet:
  //   Out: pull=down
endmodule

module Memory (
  input  CLEAR,
  input  [15:0] Memory_Address,
  input  [15:0] Data_In,
  input  Clock,
  output [15:0] Data_Out
);

  RAM #(.addrWidth(16), .dataWidth(16), .bus("separate")) ram_1 (
    .addr(Memory_Address), .din(Data_In), .data(Data_Out), .str(1'b1), .sel(1'b1), .clk(Clock), .ld(1'b1),
    .clr(CLEAR));

  // Notes on the sheet:
  //   Data_Out: pull=down
endmodule

module AddTwoNum (
  input  CLEAR,
  input  [15:0] Memory_Address,
  input  [15:0] Data_In,
  input  Clock,
  output [15:0] Data_Out
);

  Multiplexer #(.select(4), .width(16), .enable("false")) multiplexer_1 (
    .in0(16'h90f), .in1(16'haf0), .in2(16'h994c), .in3(16'hc04), .in4(16'hb80), .in5(16'h6000),
    .out(Data_Out), .sel(Memory_Address[3:0]));  // open: in6, in7, in8, in9, in10, in11, in12, in13, in14, in15

  // Notes on the sheet:
  //   Data_Out: pull=down
endmodule

module Selector (
  input  _00,
  input  _01,
  input  _10,
  input  _11,
  output [1:0] X_,
  output out_6
);

  or or_1 (X_[1], _11, _10);
  or or_2 (X_[0], _11, _01);
  or or_3 (out_6, _11, _10, _01, _00);

  // Notes on the sheet:
  //   _10: pull=down
  //   _11: pull=down
  //   _00: pull=down
  //   _01: pull=down
endmodule

module Counter (
);

  wire clock_1_out, clock_2_out, flipflo_1_out_1, flipflo_1_out_2, flipflo_2_out_2, flipflo_3_out_1,
       flipflo_3_out_2, nand_1_out, nand_2_out, nand_3_out, nand_4_out, nand_5_out, nand_6_out, nand_7_out,
       nand_8_out, nand_9_out, nand_10_out, nand_11_out, nand_12_out, nand_13_out, nand_14_out, nand_15_out;

  Clock clock_1 (.out(clock_1_out));
  Clock clock_2 (.out(clock_2_out));
  LED led_1 (.in(flipflo_1_out_2));
  FlipFlo flipflo_1 (.in_1(flipflo_1_out_2), .sync(clock_1_out), .out_1(flipflo_1_out_1), .out_2(flipflo_1_out_2));
  LED led_2 (.in(flipflo_3_out_2));
  FlipFlo flipflo_2 (.in_1(flipflo_2_out_2), .sync(flipflo_3_out_1), .out_2(flipflo_2_out_2));  // open: out_1
  FlipFlo flipflo_3 (.in_1(flipflo_3_out_2), .sync(flipflo_1_out_1), .out_1(flipflo_3_out_1), .out_2(flipflo_3_out_2));
  nand nand_1 (nand_1_out, nand_5_out, clock_2_out);
  nand nand_2 (nand_2_out, clock_2_out, nand_3_out);
  nand nand_3 (nand_3_out, nand_5_out, nand_5_out);
  LED led_3 (.in(flipflo_2_out_2));
  nand nand_4 (nand_4_out, nand_1_out, nand_5_out);
  nand nand_5 (nand_5_out, nand_4_out, nand_2_out);
  nand nand_6 (nand_6_out, nand_10_out, nand_4_out);
  nand nand_7 (nand_7_out, nand_4_out, nand_8_out);
  nand nand_8 (nand_8_out, nand_10_out, nand_10_out);
  nand nand_9 (nand_9_out, nand_6_out, nand_10_out);
  nand nand_10 (nand_10_out, nand_9_out, nand_7_out);
  nand nand_11 (nand_11_out, nand_15_out, nand_15_out);
  nand nand_12 (nand_12_out, nand_15_out, nand_9_out);
  nand nand_13 (nand_13_out, nand_9_out, nand_11_out);
  nand nand_14 (nand_14_out, nand_12_out, nand_15_out);
  nand nand_15 (nand_15_out, nand_14_out, nand_13_out);
endmodule

module FlipFlo (
  input  in_1,
  input  sync,
  output out_1,
  output out_2
);

  wire nand_1_out, nand_2_out, nand_3_out;

  nand nand_1 (nand_1_out, in_1, sync);
  nand nand_2 (nand_2_out, sync, nand_3_out);
  nand nand_3 (nand_3_out, in_1, in_1);
  nand nand_4 (out_1, nand_1_out, out_2);
  nand nand_5 (out_2, out_1, nand_2_out);
endmodule

module _2_X_7_seg (
  input  [15:0] in_1,
  output out_2,
  output out_3,
  output out_4,
  output out_5,
  output out_6,
  output out_7,
  output out_8,
  output out_9,
  output out_10,
  output out_11,
  output out_12,
  output out_13,
  output out_14,
  output out_15,
  output out_16,
  output out_17
);

  wire [15:0] sevenseg_2_out_6;

  SevenSeg sevenseg_1 (
    .Input(sevenseg_2_out_6), .out_2(out_2), .out_3(out_3), .out_4(out_4), .out_5(out_5), .out_7(out_10),
    .out_8(out_11), .out_9(out_12), .out_10(out_13));  // open: out_6
  SevenSeg sevenseg_2 (
    .Input(in_1), .out_6(sevenseg_2_out_6), .out_2(out_6), .out_3(out_7), .out_4(out_8), .out_5(out_9),
    .out_7(out_14), .out_8(out_15), .out_9(out_16), .out_10(out_17));

  // Notes on the sheet:
  //   in_1: pull=down
endmodule

module _3_X_7_seg (
  input  [15:0] in_1,
  output out_2,
  output out_3,
  output out_4,
  output out_5,
  output out_6,
  output out_7,
  output out_8,
  output out_9,
  output out_10,
  output out_11,
  output out_12,
  output out_13,
  output out_14,
  output out_15,
  output out_16,
  output out_17,
  output out_18,
  output out_19,
  output out_20,
  output out_21,
  output out_22,
  output out_23,
  output out_24,
  output out_25
);

  wire [15:0] sevenseg_2_out_6, sevenseg_3_out_6;

  SevenSeg sevenseg_1 (
    .Input(sevenseg_2_out_6), .out_2(out_2), .out_3(out_3), .out_4(out_4), .out_5(out_5), .out_7(out_14),
    .out_8(out_15), .out_9(out_16), .out_10(out_17));  // open: out_6
  SevenSeg sevenseg_2 (
    .Input(sevenseg_3_out_6), .out_6(sevenseg_2_out_6), .out_2(out_6), .out_3(out_7), .out_4(out_8),
    .out_5(out_9), .out_7(out_18), .out_8(out_19), .out_9(out_20), .out_10(out_21));
  SevenSeg sevenseg_3 (
    .Input(in_1), .out_6(sevenseg_3_out_6), .out_2(out_10), .out_3(out_11), .out_4(out_12), .out_5(out_13),
    .out_7(out_22), .out_8(out_23), .out_9(out_24), .out_10(out_25));

  // Notes on the sheet:
  //   in_1: pull=down
endmodule

module _6_X_7_seg (
  input  [15:0] in_1,
  output out_2,
  output out_3,
  output out_4,
  output out_5,
  output out_6,
  output out_7,
  output out_8,
  output out_9,
  output out_10,
  output out_11,
  output out_12,
  output out_13,
  output out_14,
  output out_15,
  output out_16,
  output out_17,
  output out_18,
  output out_19,
  output out_20,
  output out_21,
  output out_22,
  output out_23,
  output out_24,
  output out_25,
  output out_26,
  output out_27,
  output out_28,
  output out_29,
  output out_30,
  output out_31,
  output out_32,
  output out_33,
  output out_34,
  output out_35,
  output out_36,
  output out_37,
  output out_38,
  output out_39,
  output out_40,
  output out_41,
  output out_42,
  output out_43,
  output out_44,
  output out_45,
  output out_46,
  output out_47,
  output out_48,
  output out_49
);

  wire [15:0] sevenseg_2_out_6, sevenseg_3_out_6, sevenseg_4_out_6, sevenseg_5_out_6, sevenseg_6_out_6;

  SevenSeg sevenseg_1 (
    .Input(sevenseg_2_out_6), .out_2(out_2), .out_3(out_3), .out_4(out_4), .out_5(out_5), .out_7(out_26),
    .out_8(out_27), .out_9(out_28), .out_10(out_29));  // open: out_6
  SevenSeg sevenseg_2 (
    .Input(sevenseg_3_out_6), .out_6(sevenseg_2_out_6), .out_2(out_6), .out_3(out_7), .out_4(out_8),
    .out_5(out_9), .out_7(out_30), .out_8(out_31), .out_9(out_32), .out_10(out_33));
  SevenSeg sevenseg_3 (
    .Input(sevenseg_4_out_6), .out_6(sevenseg_3_out_6), .out_2(out_10), .out_3(out_11), .out_4(out_12),
    .out_5(out_13), .out_7(out_34), .out_8(out_35), .out_9(out_36), .out_10(out_37));
  SevenSeg sevenseg_4 (
    .Input(sevenseg_5_out_6), .out_6(sevenseg_4_out_6), .out_2(out_14), .out_3(out_15), .out_4(out_16),
    .out_5(out_17), .out_7(out_38), .out_8(out_39), .out_9(out_40), .out_10(out_41));
  SevenSeg sevenseg_5 (
    .Input(sevenseg_6_out_6), .out_6(sevenseg_5_out_6), .out_2(out_18), .out_3(out_19), .out_4(out_20),
    .out_5(out_21), .out_7(out_42), .out_8(out_43), .out_9(out_44), .out_10(out_45));
  SevenSeg sevenseg_6 (
    .Input(in_1), .out_6(sevenseg_6_out_6), .out_2(out_22), .out_3(out_23), .out_4(out_24), .out_5(out_25),
    .out_7(out_46), .out_8(out_47), .out_9(out_48), .out_10(out_49));

  // Notes on the sheet:
  //   in_1: pull=down
endmodule

module SevenSeg (
  input  [15:0] Input,
  output out_2,
  output out_3,
  output out_4,
  output out_5,
  output [15:0] out_6,
  output out_7,
  output out_8,
  output out_9,
  output out_10
);

  wire [15:0] divider_1_rem;

  Divider #(.width(16)) divider_1 (.a(Input), .b(16'ha), .out(out_6), .rem(divider_1_rem));  // open: upper
  SevenSegWiring sevensegwiring_1 (
    .Out__the_segment_to_light_up({out_9, out_8, out_7, out_5, out_4, out_3, out_2}),
    .Input__The_number_to_display(divider_1_rem[3:0]));
  Register #(.width(16), .trigger("high")) register_1 (.D(divider_1_rem), .clk(1'b1));  // open: en, Q, clr

  assign out_10 = 1'b0;
endmodule

module SevenSegWiring (
  input  [3:0] Input__The_number_to_display,
  output [6:0] Out__the_segment_to_light_up
);

  wire decoder_1_out0, decoder_1_out1, decoder_1_out2, decoder_1_out3, decoder_1_out4, decoder_1_out5,
       decoder_1_out6, decoder_1_out7, decoder_1_out8, decoder_1_out9;

  Decoder #(.select(4), .disabled(0), .enable("false")) decoder_1 (
    .out0(decoder_1_out0), .out1(decoder_1_out1), .out2(decoder_1_out2), .out3(decoder_1_out3),
    .out4(decoder_1_out4), .out5(decoder_1_out5), .out6(decoder_1_out6), .out7(decoder_1_out7),
    .out8(decoder_1_out8), .out9(decoder_1_out9), .sel(Input__The_number_to_display));  // open: out10, out11, out12, out13, out14, out15
  or _6 (Out__the_segment_to_light_up[6], decoder_1_out0, decoder_1_out1, decoder_1_out3, decoder_1_out4, decoder_1_out5, decoder_1_out6, decoder_1_out7, decoder_1_out8, decoder_1_out9);
  or _5 (Out__the_segment_to_light_up[5], decoder_1_out0, decoder_1_out2, decoder_1_out3, decoder_1_out5, decoder_1_out6, decoder_1_out8);
  or _4 (Out__the_segment_to_light_up[4], decoder_1_out0, decoder_1_out2, decoder_1_out6, decoder_1_out8);
  or _3 (Out__the_segment_to_light_up[3], decoder_1_out0, decoder_1_out1, decoder_1_out2, decoder_1_out3, decoder_1_out4, decoder_1_out7, decoder_1_out8, decoder_1_out9);
  or _2 (Out__the_segment_to_light_up[2], decoder_1_out0, decoder_1_out2, decoder_1_out3, decoder_1_out5, decoder_1_out6, decoder_1_out7, decoder_1_out8, decoder_1_out9);
  or _1 (Out__the_segment_to_light_up[1], decoder_1_out0, decoder_1_out4, decoder_1_out5, decoder_1_out6, decoder_1_out8, decoder_1_out9);
  or _0 (Out__the_segment_to_light_up[0], decoder_1_out2, decoder_1_out3, decoder_1_out4, decoder_1_out5, decoder_1_out6, decoder_1_out8, decoder_1_out9);

  // Notes on the sheet:
  //   Out__the_segment_to_light_up: pull=down
endmodule
