// Logisim project Tools.circ as structural Verilog: 26 circuits, main circuit 2X4 Mux
module _2X4_Mux (
  input  Sel_1,
  input  Sel_2,
  input  A,
  input  B,
  input  C,
  input  D,
  output Output
);

  wire and_1_out, and_2_out, and_3_out, and_4_out, and_5_out, and_6_out, not_1_out, not_2_out, or_1_out,
       or_2_out;

  not not_1 (not_1_out, Sel_1);
  and and_1 (and_1_out, not_1_out, A);
  and and_2 (and_2_out, Sel_1, B);
  and and_3 (and_3_out, Sel_1, C);
  and and_4 (and_4_out, not_1_out, D);
  or or_1 (or_1_out, and_1_out, and_2_out);
  or or_2 (or_2_out, and_3_out, and_4_out);
  not not_2 (not_2_out, Sel_2);
  and and_5 (and_5_out, not_2_out, or_1_out);
  and and_6 (and_6_out, Sel_2, or_2_out);
  or or_3 (Output, and_5_out, and_6_out);
endmodule

module _2x4_Demux (
  input  Sel_2,
  input  Sel_1,
  input  Input,
  output Output_A,
  output Output_B,
  output Output_C,
  output Output_D
);

  wire and_1_out, and_2_out, not_1_out, not_2_out;

  not not_1 (not_1_out, Sel_2);
  not not_2 (not_2_out, Sel_1);
  and and_1 (and_1_out, not_1_out, Input);
  and and_2 (and_2_out, Sel_2, Input);
  and and_3 (Output_A, not_2_out, and_1_out);
  and and_4 (Output_B, Sel_1, and_1_out);
  and and_5 (Output_C, not_2_out, and_2_out);
  and and_6 (Output_D, Sel_1, and_2_out);
endmodule

module Adder (
  input  CarryIn,
  input  A,
  input  B,
  output Output,
  output CarryOut
);

  wire and_1_out, and_2_out, xor_1_out;

  and and_1 (and_1_out, CarryIn, xor_1_out);
  xor xor_1 (xor_1_out, A, B);
  and and_2 (and_2_out, A, B);
  xor xor_2 (Output, CarryIn, xor_1_out);
  or or_1 (CarryOut, and_1_out, and_2_out);
endmodule

module Adder_thin (
  input  CarryIn,
  input  A,
  input  B,
  output Output,
  output CarryOut
);

  wire and_1_out, and_2_out, xor_1_out;

  xor xor_1 (xor_1_out, A, B);
  and and_1 (and_1_out, A, B);
  xor xor_2 (Output, CarryIn, xor_1_out);
  and and_2 (and_2_out, CarryIn, xor_1_out);
  or or_1 (CarryOut, and_2_out, and_1_out);
endmodule

module _2_Input_Mux (
  input  Sel,
  input  A,
  input  B,
  output Output,
  output Sel_out
);

  wire and_1_out, and_2_out, not_1_out;

  Pull_Resistor pull_resistor_1 (.node(Sel));
  not not_1 (not_1_out, Sel);
  and and_1 (and_1_out, not_1_out, A);
  or or_1 (Output, and_1_out, and_2_out);
  and and_2 (and_2_out, Sel, B);

  assign Sel_out = Sel;
endmodule

module _4_1_Mux_v2 (
  input  Sel_2,
  input  Sel_1,
  input  Input_A,
  input  Input_B,
  input  Input_C,
  input  Input_D,
  output Out,
  output Sel2_out,
  output Sel1_out
);

  wire n2_input_mux_1_output, n2_input_mux_1_sel_out, n2_input_mux_2_output;

  _2_Input_Mux u_2_input_mux_1 (
    .A(Input_A), .B(Input_B), .Output(n2_input_mux_1_output), .Sel(Sel_2), .Sel_out(n2_input_mux_1_sel_out));
  _2_Input_Mux u_2_input_mux_2 (
    .A(Input_C), .B(Input_D), .Output(n2_input_mux_2_output), .Sel(n2_input_mux_1_sel_out), .Sel_out(Sel2_out));
  _2_Input_Mux u_2_input_mux_3 (
    .A(n2_input_mux_1_output), .B(n2_input_mux_2_output), .Output(Out), .Sel(Sel_1), .Sel_out(Sel1_out));
endmodule

module _2_Input_Demux (
  input  Sel_1,
  input  Input,
  output Output_A,
  output Output_B,
  output SelOut
);

  wire not_1_out;

  not not_1 (not_1_out, Sel_1);
  and and_1 (Output_A, not_1_out, Input);
  and and_2 (Output_B, Sel_1, Input);

  assign SelOut = Sel_1;
endmodule

module _4_1_Demux_v2 (
  input  Sel_2,
  input  Sel_1,
  input  Input,
  output Output_A,
  output Output_B,
  output Output_C,
  output Output_D,
  output Sel2_Out,
  output Sel1_Out
);

  wire n2_input_demux_1_p4, n2_input_demux_1_p5;

  // _2_Input_Demux 2_input_demux_1: pin names not known; wires that end beside it: Input, Sel_2, Sel2_Out, n2_input_demux_1_p4, n2_input_demux_1_p5
  _2_Input_Demux u_2_input_demux_2 (
    .Input(n2_input_demux_1_p4), .Output_A(Output_A), .Output_B(Output_B), .Sel_1(Sel_1));  // open: SelOut
  // _2_Input_Demux 2_input_demux_3: pin names not known; wires that end beside it: n2_input_demux_1_p5, Sel1_Out, Output_C, Output_D
endmodule

module _4_Bit_Shifter (
  input  SEL,
  input  A,
  input  B,
  input  C,
  input  D,
  output Output_A,
  output Output_B,
  output Output_C,
  output Output_D
);

  wire n2_input_mux_1_sel_out, n2_input_mux_2_sel_out, n2_input_mux_3_sel_out;

  _2_Input_Mux u_2_input_mux_1 (.A(A), .B(B), .Output(Output_A), .Sel(SEL), .Sel_out(n2_input_mux_1_sel_out));
  _2_Input_Mux u_2_input_mux_2 (
    .A(B), .B(C), .Output(Output_B), .Sel(n2_input_mux_1_sel_out), .Sel_out(n2_input_mux_2_sel_out));
  _2_Input_Mux u_2_input_mux_3 (
    .A(C), .B(D), .Output(Output_C), .Sel(n2_input_mux_2_sel_out), .Sel_out(n2_input_mux_3_sel_out));
  _2_Input_Mux u_2_input_mux_4 (.A(D), .B(A), .Output(Output_D), .Sel(n2_input_mux_3_sel_out));  // open: Sel_out
endmodule

module _4_Bit_Barrel_Shifter (
  input  SEL1,
  input  SEL2,
  input  A,
  input  B,
  input  C,
  input  D,
  output Output_A,
  output Output_B,
  output Output_C,
  output Output_D
);

  wire n2_input_mux_1_output, n2_input_mux_1_sel_out, n2_input_mux_2_output, n2_input_mux_2_sel_out,
       n2_input_mux_3_output, n2_input_mux_3_sel_out, n2_input_mux_4_output, n2_input_mux_5_sel_out,
       n2_input_mux_6_sel_out, n2_input_mux_7_sel_out;

  _2_Input_Mux u_2_input_mux_1 (
    .A(A), .B(B), .Output(n2_input_mux_1_output), .Sel(SEL1), .Sel_out(n2_input_mux_1_sel_out));
  _2_Input_Mux u_2_input_mux_2 (
    .A(B), .B(C), .Output(n2_input_mux_2_output), .Sel(n2_input_mux_1_sel_out),
    .Sel_out(n2_input_mux_2_sel_out));
  _2_Input_Mux u_2_input_mux_3 (
    .A(C), .B(D), .Output(n2_input_mux_3_output), .Sel(n2_input_mux_2_sel_out),
    .Sel_out(n2_input_mux_3_sel_out));
  _2_Input_Mux u_2_input_mux_4 (
    .A(D), .B(A), .Output(n2_input_mux_4_output), .Sel(n2_input_mux_3_sel_out));  // open: Sel_out
  _2_Input_Mux u_2_input_mux_5 (
    .A(n2_input_mux_1_output), .B(n2_input_mux_3_output), .Output(Output_A), .Sel(SEL2),
    .Sel_out(n2_input_mux_5_sel_out));
  _2_Input_Mux u_2_input_mux_6 (
    .A(n2_input_mux_2_output), .B(n2_input_mux_4_output), .Output(Output_B), .Sel(n2_input_mux_5_sel_out),
    .Sel_out(n2_input_mux_6_sel_out));
  _2_Input_Mux u_2_input_mux_7 (
    .A(n2_input_mux_3_output), .B(n2_input_mux_1_output), .Output(Output_C), .Sel(n2_input_mux_6_sel_out),
    .Sel_out(n2_input_mux_7_sel_out));
  _2_Input_Mux u_2_input_mux_8 (
    .A(n2_input_mux_4_output), .B(n2_input_mux_2_output), .Output(Output_D), .Sel(n2_input_mux_7_sel_out));  // open: Sel_out
endmodule

module _4_bit_OR (
  input  in_1,
  input  in_2,
  input  in_3,
  input  in_4,
  input  in_5,
  input  in_6,
  input  in_7,
  input  in_8,
  output out_9,
  output out_10,
  output out_11,
  output out_12
);

  or or_1 (out_9, in_1, in_2);
  or or_2 (out_10, in_3, in_4);
  or or_3 (out_11, in_5, in_6);
  or or_4 (out_12, in_7, in_8);
endmodule

module _4_bit_AND (
  input  in_1,
  input  in_2,
  input  in_3,
  input  in_4,
  input  in_5,
  input  in_6,
  input  in_7,
  input  in_8,
  output out_9,
  output out_10,
  output out_11,
  output out_12
);

  and and_1 (out_9, in_1, in_2);
  and and_2 (out_10, in_3, in_4);
  and and_3 (out_11, in_5, in_6);
  and and_4 (out_12, in_7, in_8);
endmodule

module _4_bit_ALU (
  input  Sel2,
  input  Sel1,
  input  InvertA,
  input  InvertB,
  input  A1,
  input  B1,
  input  A2,
  input  B2,
  input  A3,
  input  B3,
  input  A4,
  input  B4,
  output Output_1,
  output Output_2,
  output Output_3,
  output Output_4,
  output CarryOut
);

  wire adder_thin_1_carryout, adder_thin_1_output, adder_thin_2_carryout, adder_thin_2_output,
       adder_thin_3_carryout, adder_thin_3_output, adder_thin_4_output, n2_input_mux_1_output,
       n2_input_mux_1_sel_out, n2_input_mux_2_output, n2_input_mux_2_sel_out, n2_input_mux_3_output,
       n2_input_mux_3_sel_out, n2_input_mux_4_output, n2_input_mux_5_output, n2_input_mux_5_sel_out,
       n2_input_mux_6_output, n2_input_mux_6_sel_out, n2_input_mux_7_output, n2_input_mux_7_sel_out,
       n2_input_mux_8_output, n4_1_mux_v2_1_sel1_out, n4_1_mux_v2_1_sel2_out, n4_1_mux_v2_2_sel1_out,
       n4_1_mux_v2_2_sel2_out, n4_1_mux_v2_3_sel1_out, n4_1_mux_v2_3_sel2_out, n4_bit_and_1_out_9,
       n4_bit_and_1_out_10, n4_bit_and_1_out_11, n4_bit_and_1_out_12, n4_bit_barrel_shifter_1_output_a,
       n4_bit_barrel_shifter_1_output_b, n4_bit_barrel_shifter_1_output_c, n4_bit_barrel_shifter_1_output_d,
       n4_bit_or_1_out_9, n4_bit_or_1_out_10, n4_bit_or_1_out_11, n4_bit_or_1_out_12, not_1_out, not_2_out,
       not_3_out, not_4_out, not_5_out, not_6_out, not_7_out, not_8_out;

  _2_Input_Mux u_2_input_mux_1 (
    .A(A1), .B(not_1_out), .Output(n2_input_mux_1_output), .Sel(InvertA), .Sel_out(n2_input_mux_1_sel_out));
  not not_1 (not_1_out, A1);
  _2_Input_Mux u_2_input_mux_2 (
    .A(A2), .B(not_2_out), .Output(n2_input_mux_2_output), .Sel(n2_input_mux_1_sel_out),
    .Sel_out(n2_input_mux_2_sel_out));
  not not_2 (not_2_out, A2);
  _2_Input_Mux u_2_input_mux_3 (
    .A(A3), .B(not_3_out), .Output(n2_input_mux_3_output), .Sel(n2_input_mux_2_sel_out),
    .Sel_out(n2_input_mux_3_sel_out));
  not not_3 (not_3_out, A3);
  _2_Input_Mux u_2_input_mux_4 (
    .A(A4), .B(not_4_out), .Output(n2_input_mux_4_output), .Sel(n2_input_mux_3_sel_out));  // open: Sel_out
  not not_4 (not_4_out, A4);
  not not_5 (not_5_out, B1);
  not not_6 (not_6_out, B2);
  not not_7 (not_7_out, B3);
  not not_8 (not_8_out, B4);
  _2_Input_Mux u_2_input_mux_5 (
    .A(B1), .B(not_5_out), .Output(n2_input_mux_5_output), .Sel(InvertB), .Sel_out(n2_input_mux_5_sel_out));
  _2_Input_Mux u_2_input_mux_6 (
    .A(B2), .B(not_6_out), .Output(n2_input_mux_6_output), .Sel(n2_input_mux_5_sel_out),
    .Sel_out(n2_input_mux_6_sel_out));
  _2_Input_Mux u_2_input_mux_7 (
    .A(B3), .B(not_7_out), .Output(n2_input_mux_7_output), .Sel(n2_input_mux_6_sel_out),
    .Sel_out(n2_input_mux_7_sel_out));
  _2_Input_Mux u_2_input_mux_8 (
    .A(B4), .B(not_8_out), .Output(n2_input_mux_8_output), .Sel(n2_input_mux_7_sel_out));  // open: Sel_out
  _4_Bit_Barrel_Shifter u_4_bit_barrel_shifter_1 (
    .A(n2_input_mux_1_output), .B(n2_input_mux_2_output), .C(n2_input_mux_3_output),
    .D(n2_input_mux_4_output), .Output_A(n4_bit_barrel_shifter_1_output_a),
    .Output_B(n4_bit_barrel_shifter_1_output_b), .Output_C(n4_bit_barrel_shifter_1_output_c),
    .Output_D(n4_bit_barrel_shifter_1_output_d), .SEL1(n2_input_mux_5_output), .SEL2(n2_input_mux_6_output));
  _4_bit_AND u_4_bit_and_1 (
    .in_1(n2_input_mux_1_output), .in_2(n2_input_mux_5_output), .in_3(n2_input_mux_2_output),
    .in_4(n2_input_mux_6_output), .in_5(n2_input_mux_3_output), .in_6(n2_input_mux_7_output),
    .in_7(n2_input_mux_4_output), .in_8(n2_input_mux_8_output), .out_9(n4_bit_and_1_out_9),
    .out_10(n4_bit_and_1_out_10), .out_11(n4_bit_and_1_out_11), .out_12(n4_bit_and_1_out_12));
  _4_bit_OR u_4_bit_or_1 (
    .in_1(n2_input_mux_1_output), .in_2(n2_input_mux_5_output), .in_3(n2_input_mux_2_output),
    .in_4(n2_input_mux_6_output), .in_5(n2_input_mux_3_output), .in_6(n2_input_mux_7_output),
    .in_7(n2_input_mux_4_output), .in_8(n2_input_mux_8_output), .out_9(n4_bit_or_1_out_9),
    .out_10(n4_bit_or_1_out_10), .out_11(n4_bit_or_1_out_11), .out_12(n4_bit_or_1_out_12));
  Adder_thin adder_thin_1 (
    .CarryIn(InvertB), .A(n2_input_mux_1_output), .B(n2_input_mux_5_output), .Output(adder_thin_1_output),
    .CarryOut(adder_thin_1_carryout));
  Adder_thin adder_thin_2 (
    .CarryIn(adder_thin_1_carryout), .A(n2_input_mux_2_output), .B(n2_input_mux_6_output),
    .Output(adder_thin_2_output), .CarryOut(adder_thin_2_carryout));
  Adder_thin adder_thin_3 (
    .CarryIn(adder_thin_2_carryout), .A(n2_input_mux_3_output), .B(n2_input_mux_7_output),
    .Output(adder_thin_3_output), .CarryOut(adder_thin_3_carryout));
  Adder_thin adder_thin_4 (
    .CarryIn(adder_thin_3_carryout), .A(n2_input_mux_4_output), .B(n2_input_mux_8_output),
    .Output(adder_thin_4_output), .CarryOut(CarryOut));
  _4_1_Mux_v2 u_4_1_mux_v2_1 (
    .Input_A(n4_bit_barrel_shifter_1_output_a), .Input_B(n4_bit_and_1_out_9), .Input_C(n4_bit_or_1_out_9),
    .Input_D(adder_thin_1_output), .Out(Output_1), .Sel_2(Sel2), .Sel_1(Sel1),
    .Sel2_out(n4_1_mux_v2_1_sel2_out), .Sel1_out(n4_1_mux_v2_1_sel1_out));
  _4_1_Mux_v2 u_4_1_mux_v2_2 (
    .Input_A(n4_bit_barrel_shifter_1_output_b), .Input_B(n4_bit_and_1_out_10), .Input_C(n4_bit_or_1_out_10),
    .Input_D(adder_thin_2_output), .Out(Output_2), .Sel_2(n4_1_mux_v2_1_sel2_out),
    .Sel_1(n4_1_mux_v2_1_sel1_out), .Sel2_out(n4_1_mux_v2_2_sel2_out), .Sel1_out(n4_1_mux_v2_2_sel1_out));
  _4_1_Mux_v2 u_4_1_mux_v2_3 (
    .Input_A(n4_bit_barrel_shifter_1_output_c), .Input_B(n4_bit_and_1_out_11), .Input_C(n4_bit_or_1_out_11),
    .Input_D(adder_thin_3_output), .Out(Output_3), .Sel_2(n4_1_mux_v2_2_sel2_out),
    .Sel_1(n4_1_mux_v2_2_sel1_out), .Sel2_out(n4_1_mux_v2_3_sel2_out), .Sel1_out(n4_1_mux_v2_3_sel1_out));
  _4_1_Mux_v2 u_4_1_mux_v2_4 (
    .Input_A(n4_bit_barrel_shifter_1_output_d), .Input_B(n4_bit_and_1_out_12), .Input_C(n4_bit_or_1_out_12),
    .Input_D(adder_thin_4_output), .Out(Output_4), .Sel_2(n4_1_mux_v2_3_sel2_out),
    .Sel_1(n4_1_mux_v2_3_sel1_out));  // open: Sel2_out, Sel1_out
endmodule

module _16_Bit_Adder (
  input  CarryIn,
  input  Input_1,
  input  Input_2,
  input  Input_3,
  input  Input_4,
  input  Input_5,
  input  Input_6,
  input  Input_7,
  input  Input_8,
  input  Input_9,
  input  Input_10,
  input  Input_11,
  input  Input_12,
  input  Input_13,
  input  Input_14,
  input  Input_15,
  input  Input_16,
  output Output_1,
  output Output_2,
  output Output_3,
  output Output_4,
  output Output_5,
  output Output_6,
  output Output_7,
  output Output_8,
  output CarryOut
);

  wire adder_1_carryout, adder_2_carryout, adder_3_carryout, adder_4_carryout, adder_5_carryout,
       adder_6_carryout, adder_7_carryout;

  Adder adder_1 (.CarryIn(CarryIn), .A(Input_1), .B(Input_2), .Output(Output_1), .CarryOut(adder_1_carryout));
  Adder adder_2 (.CarryIn(adder_1_carryout), .A(Input_3), .B(Input_4), .Output(Output_2), .CarryOut(adder_2_carryout));
  Adder adder_3 (.CarryIn(adder_2_carryout), .A(Input_5), .B(Input_6), .Output(Output_3), .CarryOut(adder_3_carryout));
  Adder adder_4 (.CarryIn(adder_3_carryout), .A(Input_7), .B(Input_8), .Output(Output_4), .CarryOut(adder_4_carryout));
  Adder adder_5 (.CarryIn(adder_4_carryout), .A(Input_9), .B(Input_10), .Output(Output_5), .CarryOut(adder_5_carryout));
  Adder adder_6 (
    .CarryIn(adder_5_carryout), .A(Input_11), .B(Input_12), .Output(Output_6), .CarryOut(adder_6_carryout));
  Adder adder_7 (
    .CarryIn(adder_6_carryout), .A(Input_13), .B(Input_14), .Output(Output_7), .CarryOut(adder_7_carryout));
  Adder adder_8 (.CarryIn(adder_7_carryout), .A(Input_15), .B(Input_16), .Output(Output_8), .CarryOut(CarryOut));
endmodule

module _16_4_MUX (
  input  Sel_2,
  input  Sel_1,
  input  _1A,
  input  _1B,
  input  _1C,
  input  _1D,
  input  _2A,
  input  _2B,
  input  _2C,
  input  _2D,
  input  _3A,
  input  _3B,
  input  _3C,
  input  _3D,
  input  _4A,
  input  _4B,
  input  _4C,
  input  _4D,
  output Out_1,
  output Out_2,
  output Out_3,
  output Out_4,
  output Sel2_out,
  output Sel1_out
);

  wire n2_input_mux_1_output, n2_input_mux_1_sel_out, n2_input_mux_2_sel_out, n2_input_mux_3_output,
       n2_input_mux_3_sel_out, n2_input_mux_4_output, n2_input_mux_4_sel_out, n2_input_mux_5_sel_out,
       n2_input_mux_6_output, n2_input_mux_6_sel_out, n2_input_mux_7_output, n2_input_mux_7_sel_out,
       n2_input_mux_8_sel_out, n2_input_mux_9_output, n2_input_mux_9_sel_out, n2_input_mux_10_output,
       n2_input_mux_10_sel_out, n2_input_mux_12_output;

  _2_Input_Mux u_2_input_mux_1 (
    .A(_1A), .B(_1B), .Output(n2_input_mux_1_output), .Sel(Sel_2), .Sel_out(n2_input_mux_1_sel_out));
  _2_Input_Mux u_2_input_mux_2 (
    .A(n2_input_mux_1_output), .B(n2_input_mux_3_output), .Output(Out_1), .Sel(Sel_1),
    .Sel_out(n2_input_mux_2_sel_out));
  _2_Input_Mux u_2_input_mux_3 (
    .A(_1C), .B(_1D), .Output(n2_input_mux_3_output), .Sel(n2_input_mux_1_sel_out),
    .Sel_out(n2_input_mux_3_sel_out));
  _2_Input_Mux u_2_input_mux_4 (
    .A(_2A), .B(_2B), .Output(n2_input_mux_4_output), .Sel(n2_input_mux_3_sel_out),
    .Sel_out(n2_input_mux_4_sel_out));
  _2_Input_Mux u_2_input_mux_5 (
    .A(n2_input_mux_4_output), .B(n2_input_mux_6_output), .Output(Out_2), .Sel(n2_input_mux_2_sel_out),
    .Sel_out(n2_input_mux_5_sel_out));
  _2_Input_Mux u_2_input_mux_6 (
    .A(_2C), .B(_2D), .Output(n2_input_mux_6_output), .Sel(n2_input_mux_4_sel_out),
    .Sel_out(n2_input_mux_6_sel_out));
  _2_Input_Mux u_2_input_mux_7 (
    .A(_3A), .B(_3B), .Output(n2_input_mux_7_output), .Sel(n2_input_mux_6_sel_out),
    .Sel_out(n2_input_mux_7_sel_out));
  _2_Input_Mux u_2_input_mux_8 (
    .A(n2_input_mux_7_output), .B(n2_input_mux_9_output), .Output(Out_3), .Sel(n2_input_mux_5_sel_out),
    .Sel_out(n2_input_mux_8_sel_out));
  _2_Input_Mux u_2_input_mux_9 (
    .A(_3C), .B(_3D), .Output(n2_input_mux_9_output), .Sel(n2_input_mux_7_sel_out),
    .Sel_out(n2_input_mux_9_sel_out));
  _2_Input_Mux u_2_input_mux_10 (
    .A(_4A), .B(_4B), .Output(n2_input_mux_10_output), .Sel(n2_input_mux_9_sel_out),
    .Sel_out(n2_input_mux_10_sel_out));
  _2_Input_Mux u_2_input_mux_11 (
    .A(n2_input_mux_10_output), .B(n2_input_mux_12_output), .Output(Out_4), .Sel(n2_input_mux_8_sel_out),
    .Sel_out(Sel1_out));
  _2_Input_Mux u_2_input_mux_12 (
    .A(_4C), .B(_4D), .Output(n2_input_mux_12_output), .Sel(n2_input_mux_10_sel_out), .Sel_out(Sel2_out));
endmodule

module _16_4_MUX__bundled_i_o (
  input  [1:0] Select_in,
  input  [3:0] A,
  input  [3:0] B,
  input  [3:0] C,
  input  [3:0] D,
  output [3:0] Output,
  output [1:0] Select_out
);

  _16_4_MUX u_16_4_mux_1 (
    ._1A(A[0]), ._1B(B[0]), ._1C(C[0]), ._1D(D[0]), ._2A(A[1]), ._2B(B[1]), ._2C(C[1]), ._2D(D[1]),
    ._3A(A[2]), ._3B(B[2]), ._3C(C[2]), ._3D(D[2]), ._4A(A[3]), ._4B(B[3]), ._4C(C[3]), ._4D(D[3]),
    .Out_1(Output[0]), .Out_2(Output[1]), .Out_3(Output[2]), .Out_4(Output[3]), .Sel_2(Select_in[0]),
    .Sel_1(Select_in[1]), .Sel2_out(Select_out[0]), .Sel1_out(Select_out[1]));
endmodule

module _64_16_MUX__bundled_i_o (
  input  [1:0] Select,
  input  [15:0] A,
  input  [15:0] B,
  input  [15:0] C,
  input  [15:0] D,
  output [15:0] Output,
  output [1:0] out_7
);

  wire [1:0] n16_4_mux_bundled_i_o_1_select_out, n16_4_mux_bundled_i_o_2_select_out,
       n16_4_mux_bundled_i_o_3_select_out;

  _16_4_MUX__bundled_i_o u_16_4_mux_bundled_i_o_1 (
    .A(A[3:0]), .B(B[3:0]), .C(C[3:0]), .D(D[3:0]), .Output(Output[3:0]), .Select_in(Select),
    .Select_out(n16_4_mux_bundled_i_o_1_select_out));
  _16_4_MUX__bundled_i_o u_16_4_mux_bundled_i_o_2 (
    .A(A[7:4]), .B(B[7:4]), .C(C[7:4]), .D(D[7:4]), .Output(Output[7:4]),
    .Select_in(n16_4_mux_bundled_i_o_1_select_out), .Select_out(n16_4_mux_bundled_i_o_2_select_out));
  _16_4_MUX__bundled_i_o u_16_4_mux_bundled_i_o_3 (
    .A(A[11:8]), .B(B[11:8]), .C(C[11:8]), .D(D[11:8]), .Output(Output[11:8]),
    .Select_in(n16_4_mux_bundled_i_o_2_select_out), .Select_out(n16_4_mux_bundled_i_o_3_select_out));
  _16_4_MUX__bundled_i_o u_16_4_mux_bundled_i_o_4 (
    .A(A[15:12]), .B(B[15:12]), .C(C[15:12]), .D(D[15:12]), .Output(Output[15:12]),
    .Select_in(n16_4_mux_bundled_i_o_3_select_out), .Select_out(out_7));
endmodule

module _16_bit_adder__bundled_i_o (
  input  CarryIn,
  input  [15:0] A,
  input  [15:0] B,
  output [15:0] Out,
  output CarryOut
);

  wire adder_1_carryout, adder_2_carryout, adder_3_carryout, adder_4_carryout, adder_5_carryout,
       adder_6_carryout, adder_7_carryout, adder_8_carryout, adder_9_carryout, adder_10_carryout,
       adder_11_carryout, adder_12_carryout, adder_13_carryout, adder_14_carryout, adder_15_carryout;

  Adder adder_1 (.CarryIn(CarryIn), .A(A[0]), .B(B[0]), .Output(Out[0]), .CarryOut(adder_1_carryout));
  Adder adder_2 (.CarryIn(adder_1_carryout), .A(A[1]), .B(B[1]), .Output(Out[1]), .CarryOut(adder_2_carryout));
  Adder adder_3 (.CarryIn(adder_2_carryout), .A(A[2]), .B(B[2]), .Output(Out[2]), .CarryOut(adder_3_carryout));
  Adder adder_4 (.CarryIn(adder_3_carryout), .A(A[3]), .B(B[3]), .Output(Out[3]), .CarryOut(adder_4_carryout));
  Adder adder_5 (.CarryIn(adder_4_carryout), .A(A[4]), .B(B[4]), .Output(Out[4]), .CarryOut(adder_5_carryout));
  Adder adder_6 (.CarryIn(adder_5_carryout), .A(A[5]), .B(B[5]), .Output(Out[5]), .CarryOut(adder_6_carryout));
  Adder adder_7 (.CarryIn(adder_6_carryout), .A(A[6]), .B(B[6]), .Output(Out[6]), .CarryOut(adder_7_carryout));
  Adder adder_8 (.CarryIn(adder_7_carryout), .A(A[7]), .B(B[7]), .Output(Out[7]), .CarryOut(adder_8_carryout));
  Adder adder_9 (.CarryIn(adder_8_carryout), .A(A[8]), .B(B[8]), .Output(Out[8]), .CarryOut(adder_9_carryout));
  Adder adder_10 (.CarryIn(adder_9_carryout), .A(A[9]), .B(B[9]), .Output(Out[9]), .CarryOut(adder_10_carryout));
  Adder adder_11 (.CarryIn(adder_10_carryout), .A(A[10]), .B(B[10]), .Output(Out[10]), .CarryOut(adder_11_carryout));
  Adder adder_12 (.CarryIn(adder_11_carryout), .A(A[11]), .B(B[11]), .Output(Out[11]), .CarryOut(adder_12_carryout));
  Adder adder_13 (.CarryIn(adder_12_carryout), .A(A[12]), .B(B[12]), .Output(Out[12]), .CarryOut(adder_13_carryout));
  Adder adder_14 (.CarryIn(adder_13_carryout), .A(A[13]), .B(B[13]), .Output(Out[13]), .CarryOut(adder_14_carryout));
  Adder adder_15 (.CarryIn(adder_14_carryout), .A(A[14]), .B(B[14]), .Output(Out[14]), .CarryOut(adder_15_carryout));
  Adder adder_16 (.CarryIn(adder_15_carryout), .A(A[15]), .B(B[15]), .Output(Out[15]), .CarryOut(CarryOut));
  Pull_Resistor pull_resistor_1 (.node(CarryIn));

  // Notes on the sheet:
  //   CarryIn: pull=down
endmodule

module _16_bit_and__bundled_i_o (
  input  [15:0] A,
  input  [15:0] B,
  output [15:0] Out
);

  and and_1 (Out[0], A[0], B[0]);
  and and_2 (Out[1], A[1], B[1]);
  and and_3 (Out[2], A[2], B[2]);
  and and_4 (Out[3], A[3], B[3]);
  and and_5 (Out[4], A[4], B[4]);
  and and_6 (Out[5], A[5], B[5]);
  and and_7 (Out[6], A[6], B[6]);
  and and_8 (Out[7], A[7], B[7]);
  and and_9 (Out[8], A[8], B[8]);
  and and_10 (Out[9], A[9], B[9]);
  and and_11 (Out[10], A[10], B[10]);
  and and_12 (Out[11], A[11], B[11]);
  and and_13 (Out[12], A[12], B[12]);
  and and_14 (Out[13], A[13], B[13]);
  and and_15 (Out[14], A[14], B[14]);
  and and_16 (Out[15], A[15], B[15]);
endmodule

module _16_bit_or__bundled_i_o (
  input  [15:0] A,
  input  [15:0] B,
  output [15:0] Out
);

  or or_1 (Out[0], A[0], B[0]);
  or or_2 (Out[1], A[1], B[1]);
  or or_3 (Out[2], A[2], B[2]);
  or or_4 (Out[3], A[3], B[3]);
  or or_5 (Out[4], A[4], B[4]);
  or or_6 (Out[5], A[5], B[5]);
  or or_7 (Out[6], A[6], B[6]);
  or or_8 (Out[7], A[7], B[7]);
  or or_9 (Out[8], A[8], B[8]);
  or or_10 (Out[9], A[9], B[9]);
  or or_11 (Out[10], A[10], B[10]);
  or or_12 (Out[11], A[11], B[11]);
  or or_13 (Out[12], A[12], B[12]);
  or or_14 (Out[13], A[13], B[13]);
  or or_15 (Out[14], A[14], B[14]);
  or or_16 (Out[15], A[15], B[15]);
endmodule

module _16_bit_inverter__bundled_i_o (
  input  Invert_in,
  input  [15:0] Input,
  output [15:0] Output
);

  wire n2_input_mux_1_sel_out, n2_input_mux_2_sel_out, n2_input_mux_3_sel_out, n2_input_mux_5_sel_out,
       n2_input_mux_6_sel_out, n2_input_mux_7_sel_out, n2_input_mux_9_sel_out, n2_input_mux_10_sel_out,
       n2_input_mux_11_sel_out, n2_input_mux_13_sel_out, n2_input_mux_14_sel_out, n2_input_mux_15_sel_out,
       not_1_out, not_2_out, not_3_out, not_4_out, not_5_out, not_6_out, not_7_out, not_8_out, not_9_out,
       not_10_out, not_11_out, not_12_out, not_13_out, not_14_out, not_15_out, not_16_out;

  _2_Input_Mux u_2_input_mux_1 (
    .A(Input[15]), .B(not_1_out), .Output(Output[15]), .Sel(Invert_in), .Sel_out(n2_input_mux_1_sel_out));
  not not_1 (not_1_out, Input[15]);
  _2_Input_Mux u_2_input_mux_2 (
    .A(Input[14]), .B(not_2_out), .Output(Output[14]), .Sel(n2_input_mux_1_sel_out),
    .Sel_out(n2_input_mux_2_sel_out));
  not not_2 (not_2_out, Input[14]);
  _2_Input_Mux u_2_input_mux_3 (
    .A(Input[13]), .B(not_3_out), .Output(Output[13]), .Sel(n2_input_mux_2_sel_out),
    .Sel_out(n2_input_mux_3_sel_out));
  not not_3 (not_3_out, Input[13]);
  _2_Input_Mux u_2_input_mux_4 (
    .A(Input[12]), .B(not_4_out), .Output(Output[12]), .Sel(n2_input_mux_3_sel_out));  // open: Sel_out
  not not_4 (not_4_out, Input[12]);
  not not_5 (not_5_out, Input[11]);
  not not_6 (not_6_out, Input[10]);
  not not_7 (not_7_out, Input[9]);
  not not_8 (not_8_out, Input[8]);
  _2_Input_Mux u_2_input_mux_5 (
    .A(Input[11]), .B(not_5_out), .Output(Output[11]), .Sel(Invert_in), .Sel_out(n2_input_mux_5_sel_out));
  _2_Input_Mux u_2_input_mux_6 (
    .A(Input[10]), .B(not_6_out), .Output(Output[10]), .Sel(n2_input_mux_5_sel_out),
    .Sel_out(n2_input_mux_6_sel_out));
  _2_Input_Mux u_2_input_mux_7 (
    .A(Input[9]), .B(not_7_out), .Output(Output[9]), .Sel(n2_input_mux_6_sel_out),
    .Sel_out(n2_input_mux_7_sel_out));
  _2_Input_Mux u_2_input_mux_8 (
    .A(Input[8]), .B(not_8_out), .Output(Output[8]), .Sel(n2_input_mux_7_sel_out));  // open: Sel_out
  not not_9 (not_9_out, Input[7]);
  not not_10 (not_10_out, Input[6]);
  not not_11 (not_11_out, Input[5]);
  not not_12 (not_12_out, Input[4]);
  _2_Input_Mux u_2_input_mux_9 (
    .A(Input[7]), .B(not_9_out), .Output(Output[7]), .Sel(Invert_in), .Sel_out(n2_input_mux_9_sel_out));
  _2_Input_Mux u_2_input_mux_10 (
    .A(Input[6]), .B(not_10_out), .Output(Output[6]), .Sel(n2_input_mux_9_sel_out),
    .Sel_out(n2_input_mux_10_sel_out));
  _2_Input_Mux u_2_input_mux_11 (
    .A(Input[5]), .B(not_11_out), .Output(Output[5]), .Sel(n2_input_mux_10_sel_out),
    .Sel_out(n2_input_mux_11_sel_out));
  _2_Input_Mux u_2_input_mux_12 (
    .A(Input[4]), .B(not_12_out), .Output(Output[4]), .Sel(n2_input_mux_11_sel_out));  // open: Sel_out
  _2_Input_Mux u_2_input_mux_13 (
    .A(Input[3]), .B(not_13_out), .Output(Output[3]), .Sel(Invert_in), .Sel_out(n2_input_mux_13_sel_out));
  not not_13 (not_13_out, Input[3]);
  _2_Input_Mux u_2_input_mux_14 (
    .A(Input[2]), .B(not_14_out), .Output(Output[2]), .Sel(n2_input_mux_13_sel_out),
    .Sel_out(n2_input_mux_14_sel_out));
  not not_14 (not_14_out, Input[2]);
  _2_Input_Mux u_2_input_mux_15 (
    .A(Input[1]), .B(not_15_out), .Output(Output[1]), .Sel(n2_input_mux_14_sel_out),
    .Sel_out(n2_input_mux_15_sel_out));
  not not_15 (not_15_out, Input[1]);
  _2_Input_Mux u_2_input_mux_16 (
    .A(Input[0]), .B(not_16_out), .Output(Output[0]), .Sel(n2_input_mux_15_sel_out));  // open: Sel_out
  not not_16 (not_16_out, Input[0]);
endmodule

module _16_bit_shifter__bundled_i_o (
  input  [3:0] in_1,
  input  [15:0] Input,
  output [15:0] Output
);

  wire n2_input_mux_1_output, n2_input_mux_1_sel_out, n2_input_mux_2_output, n2_input_mux_2_sel_out,
       n2_input_mux_3_output, n2_input_mux_3_sel_out, n2_input_mux_4_output, n2_input_mux_4_sel_out,
       n2_input_mux_5_output, n2_input_mux_5_sel_out, n2_input_mux_6_output, n2_input_mux_6_sel_out,
       n2_input_mux_7_output, n2_input_mux_7_sel_out, n2_input_mux_8_output, n2_input_mux_8_sel_out,
       n2_input_mux_9_output, n2_input_mux_9_sel_out, n2_input_mux_10_output, n2_input_mux_10_sel_out,
       n2_input_mux_11_output, n2_input_mux_11_sel_out, n2_input_mux_12_output, n2_input_mux_12_sel_out,
       n2_input_mux_13_output, n2_input_mux_13_sel_out, n2_input_mux_14_output, n2_input_mux_14_sel_out,
       n2_input_mux_15_output, n2_input_mux_15_sel_out, n2_input_mux_16_output, n2_input_mux_17_output,
       n2_input_mux_17_sel_out, n2_input_mux_18_output, n2_input_mux_18_sel_out, n2_input_mux_19_output,
       n2_input_mux_19_sel_out, n2_input_mux_20_output, n2_input_mux_20_sel_out, n2_input_mux_21_output,
       n2_input_mux_21_sel_out, n2_input_mux_22_output, n2_input_mux_22_sel_out, n2_input_mux_23_output,
       n2_input_mux_23_sel_out, n2_input_mux_24_output, n2_input_mux_24_sel_out, n2_input_mux_25_output,
       n2_input_mux_25_sel_out, n2_input_mux_26_output, n2_input_mux_26_sel_out, n2_input_mux_27_output,
       n2_input_mux_27_sel_out, n2_input_mux_28_output, n2_input_mux_28_sel_out, n2_input_mux_29_output,
       n2_input_mux_29_sel_out, n2_input_mux_30_output, n2_input_mux_30_sel_out, n2_input_mux_31_output,
       n2_input_mux_31_sel_out, n2_input_mux_32_output, n2_input_mux_33_output, n2_input_mux_33_sel_out,
       n2_input_mux_34_output, n2_input_mux_34_sel_out, n2_input_mux_35_output, n2_input_mux_35_sel_out,
       n2_input_mux_36_output, n2_input_mux_36_sel_out, n2_input_mux_37_output, n2_input_mux_37_sel_out,
       n2_input_mux_38_output, n2_input_mux_38_sel_out, n2_input_mux_39_output, n2_input_mux_39_sel_out,
       n2_input_mux_40_output, n2_input_mux_40_sel_out, n2_input_mux_41_output, n2_input_mux_41_sel_out,
       n2_input_mux_42_output, n2_input_mux_42_sel_out, n2_input_mux_43_output, n2_input_mux_43_sel_out,
       n2_input_mux_44_output, n2_input_mux_44_sel_out, n2_input_mux_45_output, n2_input_mux_45_sel_out,
       n2_input_mux_46_output, n2_input_mux_46_sel_out, n2_input_mux_47_output, n2_input_mux_47_sel_out,
       n2_input_mux_48_output, n2_input_mux_49_sel_out, n2_input_mux_50_sel_out, n2_input_mux_51_sel_out,
       n2_input_mux_52_sel_out, n2_input_mux_53_sel_out, n2_input_mux_54_sel_out, n2_input_mux_55_sel_out,
       n2_input_mux_56_sel_out, n2_input_mux_57_sel_out, n2_input_mux_58_sel_out, n2_input_mux_59_sel_out,
       n2_input_mux_60_sel_out, n2_input_mux_61_sel_out, n2_input_mux_62_sel_out, n2_input_mux_63_sel_out;

  _2_Input_Mux u_2_input_mux_1 (
    .A(Input[15]), .B(Input[14]), .Output(n2_input_mux_1_output), .Sel(in_1[0]),
    .Sel_out(n2_input_mux_1_sel_out));
  _2_Input_Mux u_2_input_mux_2 (
    .A(Input[14]), .B(Input[13]), .Output(n2_input_mux_2_output), .Sel(n2_input_mux_1_sel_out),
    .Sel_out(n2_input_mux_2_sel_out));
  _2_Input_Mux u_2_input_mux_3 (
    .A(Input[13]), .B(Input[12]), .Output(n2_input_mux_3_output), .Sel(n2_input_mux_2_sel_out),
    .Sel_out(n2_input_mux_3_sel_out));
  _2_Input_Mux u_2_input_mux_4 (
    .A(Input[12]), .B(Input[11]), .Output(n2_input_mux_4_output), .Sel(n2_input_mux_3_sel_out),
    .Sel_out(n2_input_mux_4_sel_out));
  _2_Input_Mux u_2_input_mux_5 (
    .A(Input[11]), .B(Input[10]), .Output(n2_input_mux_5_output), .Sel(n2_input_mux_4_sel_out),
    .Sel_out(n2_input_mux_5_sel_out));
  _2_Input_Mux u_2_input_mux_6 (
    .A(Input[10]), .B(Input[9]), .Output(n2_input_mux_6_output), .Sel(n2_input_mux_5_sel_out),
    .Sel_out(n2_input_mux_6_sel_out));
  _2_Input_Mux u_2_input_mux_7 (
    .A(Input[9]), .B(Input[8]), .Output(n2_input_mux_7_output), .Sel(n2_input_mux_6_sel_out),
    .Sel_out(n2_input_mux_7_sel_out));
  _2_Input_Mux u_2_input_mux_8 (
    .A(Input[8]), .B(Input[7]), .Output(n2_input_mux_8_output), .Sel(n2_input_mux_7_sel_out),
    .Sel_out(n2_input_mux_8_sel_out));
  _2_Input_Mux u_2_input_mux_9 (
    .A(Input[7]), .B(Input[6]), .Output(n2_input_mux_9_output), .Sel(n2_input_mux_8_sel_out),
    .Sel_out(n2_input_mux_9_sel_out));
  _2_Input_Mux u_2_input_mux_10 (
    .A(Input[6]), .B(Input[5]), .Output(n2_input_mux_10_output), .Sel(n2_input_mux_9_sel_out),
    .Sel_out(n2_input_mux_10_sel_out));
  _2_Input_Mux u_2_input_mux_11 (
    .A(Input[5]), .B(Input[4]), .Output(n2_input_mux_11_output), .Sel(n2_input_mux_10_sel_out),
    .Sel_out(n2_input_mux_11_sel_out));
  _2_Input_Mux u_2_input_mux_12 (
    .A(Input[4]), .B(Input[3]), .Output(n2_input_mux_12_output), .Sel(n2_input_mux_11_sel_out),
    .Sel_out(n2_input_mux_12_sel_out));
  _2_Input_Mux u_2_input_mux_13 (
    .A(Input[3]), .B(Input[2]), .Output(n2_input_mux_13_output), .Sel(n2_input_mux_12_sel_out),
    .Sel_out(n2_input_mux_13_sel_out));
  _2_Input_Mux u_2_input_mux_14 (
    .A(Input[2]), .B(Input[1]), .Output(n2_input_mux_14_output), .Sel(n2_input_mux_13_sel_out),
    .Sel_out(n2_input_mux_14_sel_out));
  _2_Input_Mux u_2_input_mux_15 (
    .A(Input[1]), .B(Input[0]), .Output(n2_input_mux_15_output), .Sel(n2_input_mux_14_sel_out),
    .Sel_out(n2_input_mux_15_sel_out));
  _2_Input_Mux u_2_input_mux_16 (
    .A(Input[0]), .B(Input[15]), .Output(n2_input_mux_16_output), .Sel(n2_input_mux_15_sel_out));  // open: Sel_out
  _2_Input_Mux u_2_input_mux_17 (
    .A(n2_input_mux_1_output), .B(n2_input_mux_3_output), .Output(n2_input_mux_17_output), .Sel(in_1[1]),
    .Sel_out(n2_input_mux_17_sel_out));
  _2_Input_Mux u_2_input_mux_18 (
    .A(n2_input_mux_2_output), .B(n2_input_mux_4_output), .Output(n2_input_mux_18_output),
    .Sel(n2_input_mux_17_sel_out), .Sel_out(n2_input_mux_18_sel_out));
  _2_Input_Mux u_2_input_mux_19 (
    .A(n2_input_mux_3_output), .B(n2_input_mux_5_output), .Output(n2_input_mux_19_output),
    .Sel(n2_input_mux_18_sel_out), .Sel_out(n2_input_mux_19_sel_out));
  _2_Input_Mux u_2_input_mux_20 (
    .A(n2_input_mux_4_output), .B(n2_input_mux_6_output), .Output(n2_input_mux_20_output),
    .Sel(n2_input_mux_19_sel_out), .Sel_out(n2_input_mux_20_sel_out));
  _2_Input_Mux u_2_input_mux_21 (
    .A(n2_input_mux_5_output), .B(n2_input_mux_7_output), .Output(n2_input_mux_21_output),
    .Sel(n2_input_mux_20_sel_out), .Sel_out(n2_input_mux_21_sel_out));
  _2_Input_Mux u_2_input_mux_22 (
    .A(n2_input_mux_6_output), .B(n2_input_mux_8_output), .Output(n2_input_mux_22_output),
    .Sel(n2_input_mux_21_sel_out), .Sel_out(n2_input_mux_22_sel_out));
  _2_Input_Mux u_2_input_mux_23 (
    .A(n2_input_mux_7_output), .B(n2_input_mux_9_output), .Output(n2_input_mux_23_output),
    .Sel(n2_input_mux_22_sel_out), .Sel_out(n2_input_mux_23_sel_out));
  _2_Input_Mux u_2_input_mux_24 (
    .A(n2_input_mux_8_output), .B(n2_input_mux_10_output), .Output(n2_input_mux_24_output),
    .Sel(n2_input_mux_23_sel_out), .Sel_out(n2_input_mux_24_sel_out));
  _2_Input_Mux u_2_input_mux_25 (
    .A(n2_input_mux_9_output), .B(n2_input_mux_11_output), .Output(n2_input_mux_25_output),
    .Sel(n2_input_mux_24_sel_out), .Sel_out(n2_input_mux_25_sel_out));
  _2_Input_Mux u_2_input_mux_26 (
    .A(n2_input_mux_10_output), .B(n2_input_mux_12_output), .Output(n2_input_mux_26_output),
    .Sel(n2_input_mux_25_sel_out), .Sel_out(n2_input_mux_26_sel_out));
  _2_Input_Mux u_2_input_mux_27 (
    .A(n2_input_mux_11_output), .B(n2_input_mux_13_output), .Output(n2_input_mux_27_output),
    .Sel(n2_input_mux_26_sel_out), .Sel_out(n2_input_mux_27_sel_out));
  _2_Input_Mux u_2_input_mux_28 (
    .A(n2_input_mux_12_output), .B(n2_input_mux_14_output), .Output(n2_input_mux_28_output),
    .Sel(n2_input_mux_27_sel_out), .Sel_out(n2_input_mux_28_sel_out));
  _2_Input_Mux u_2_input_mux_29 (
    .A(n2_input_mux_13_output), .B(n2_input_mux_15_output), .Output(n2_input_mux_29_output),
    .Sel(n2_input_mux_28_sel_out), .Sel_out(n2_input_mux_29_sel_out));
  _2_Input_Mux u_2_input_mux_30 (
    .A(n2_input_mux_14_output), .B(n2_input_mux_16_output), .Output(n2_input_mux_30_output),
    .Sel(n2_input_mux_29_sel_out), .Sel_out(n2_input_mux_30_sel_out));
  _2_Input_Mux u_2_input_mux_31 (
    .A(n2_input_mux_15_output), .B(n2_input_mux_1_output), .Output(n2_input_mux_31_output),
    .Sel(n2_input_mux_30_sel_out), .Sel_out(n2_input_mux_31_sel_out));
  _2_Input_Mux u_2_input_mux_32 (
    .A(n2_input_mux_16_output), .B(n2_input_mux_2_output), .Output(n2_input_mux_32_output),
    .Sel(n2_input_mux_31_sel_out));  // open: Sel_out
  _2_Input_Mux u_2_input_mux_33 (
    .A(n2_input_mux_17_output), .B(n2_input_mux_21_output), .Output(n2_input_mux_33_output), .Sel(in_1[2]),
    .Sel_out(n2_input_mux_33_sel_out));
  _2_Input_Mux u_2_input_mux_34 (
    .A(n2_input_mux_18_output), .B(n2_input_mux_22_output), .Output(n2_input_mux_34_output),
    .Sel(n2_input_mux_33_sel_out), .Sel_out(n2_input_mux_34_sel_out));
  _2_Input_Mux u_2_input_mux_35 (
    .A(n2_input_mux_19_output), .B(n2_input_mux_23_output), .Output(n2_input_mux_35_output),
    .Sel(n2_input_mux_34_sel_out), .Sel_out(n2_input_mux_35_sel_out));
  _2_Input_Mux u_2_input_mux_36 (
    .A(n2_input_mux_20_output), .B(n2_input_mux_24_output), .Output(n2_input_mux_36_output),
    .Sel(n2_input_mux_35_sel_out), .Sel_out(n2_input_mux_36_sel_out));
  _2_Input_Mux u_2_input_mux_37 (
    .A(n2_input_mux_21_output), .B(n2_input_mux_25_output), .Output(n2_input_mux_37_output),
    .Sel(n2_input_mux_36_sel_out), .Sel_out(n2_input_mux_37_sel_out));
  _2_Input_Mux u_2_input_mux_38 (
    .A(n2_input_mux_22_output), .B(n2_input_mux_26_output), .Output(n2_input_mux_38_output),
    .Sel(n2_input_mux_37_sel_out), .Sel_out(n2_input_mux_38_sel_out));
  _2_Input_Mux u_2_input_mux_39 (
    .A(n2_input_mux_23_output), .B(n2_input_mux_27_output), .Output(n2_input_mux_39_output),
    .Sel(n2_input_mux_38_sel_out), .Sel_out(n2_input_mux_39_sel_out));
  _2_Input_Mux u_2_input_mux_40 (
    .A(n2_input_mux_24_output), .B(n2_input_mux_28_output), .Output(n2_input_mux_40_output),
    .Sel(n2_input_mux_39_sel_out), .Sel_out(n2_input_mux_40_sel_out));
  _2_Input_Mux u_2_input_mux_41 (
    .A(n2_input_mux_25_output), .B(n2_input_mux_29_output), .Output(n2_input_mux_41_output),
    .Sel(n2_input_mux_40_sel_out), .Sel_out(n2_input_mux_41_sel_out));
  _2_Input_Mux u_2_input_mux_42 (
    .A(n2_input_mux_26_output), .B(n2_input_mux_30_output), .Output(n2_input_mux_42_output),
    .Sel(n2_input_mux_41_sel_out), .Sel_out(n2_input_mux_42_sel_out));
  _2_Input_Mux u_2_input_mux_43 (
    .A(n2_input_mux_27_output), .B(n2_input_mux_31_output), .Output(n2_input_mux_43_output),
    .Sel(n2_input_mux_42_sel_out), .Sel_out(n2_input_mux_43_sel_out));
  _2_Input_Mux u_2_input_mux_44 (
    .A(n2_input_mux_28_output), .B(n2_input_mux_32_output), .Output(n2_input_mux_44_output),
    .Sel(n2_input_mux_43_sel_out), .Sel_out(n2_input_mux_44_sel_out));
  _2_Input_Mux u_2_input_mux_45 (
    .A(n2_input_mux_29_output), .B(n2_input_mux_17_output), .Output(n2_input_mux_45_output),
    .Sel(n2_input_mux_44_sel_out), .Sel_out(n2_input_mux_45_sel_out));
  _2_Input_Mux u_2_input_mux_46 (
    .A(n2_input_mux_30_output), .B(n2_input_mux_18_output), .Output(n2_input_mux_46_output),
    .Sel(n2_input_mux_45_sel_out), .Sel_out(n2_input_mux_46_sel_out));
  _2_Input_Mux u_2_input_mux_47 (
    .A(n2_input_mux_31_output), .B(n2_input_mux_19_output), .Output(n2_input_mux_47_output),
    .Sel(n2_input_mux_46_sel_out), .Sel_out(n2_input_mux_47_sel_out));
  _2_Input_Mux u_2_input_mux_48 (
    .A(n2_input_mux_32_output), .B(n2_input_mux_20_output), .Output(n2_input_mux_48_output),
    .Sel(n2_input_mux_47_sel_out));  // open: Sel_out
  _2_Input_Mux u_2_input_mux_49 (
    .A(n2_input_mux_33_output), .B(n2_input_mux_41_output), .Output(Output[15]), .Sel(in_1[3]),
    .Sel_out(n2_input_mux_49_sel_out));
  _2_Input_Mux u_2_input_mux_50 (
    .A(n2_input_mux_34_output), .B(n2_input_mux_42_output), .Output(Output[14]),
    .Sel(n2_input_mux_49_sel_out), .Sel_out(n2_input_mux_50_sel_out));
  _2_Input_Mux u_2_input_mux_51 (
    .A(n2_input_mux_35_output), .B(n2_input_mux_43_output), .Output(Output[13]),
    .Sel(n2_input_mux_50_sel_out), .Sel_out(n2_input_mux_51_sel_out));
  _2_Input_Mux u_2_input_mux_52 (
    .A(n2_input_mux_36_output), .B(n2_input_mux_44_output), .Output(Output[12]),
    .Sel(n2_input_mux_51_sel_out), .Sel_out(n2_input_mux_52_sel_out));
  _2_Input_Mux u_2_input_mux_53 (
    .A(n2_input_mux_37_output), .B(n2_input_mux_45_output), .Output(Output[11]),
    .Sel(n2_input_mux_52_sel_out), .Sel_out(n2_input_mux_53_sel_out));
  _2_Input_Mux u_2_input_mux_54 (
    .A(n2_input_mux_38_output), .B(n2_input_mux_46_output), .Output(Output[10]),
    .Sel(n2_input_mux_53_sel_out), .Sel_out(n2_input_mux_54_sel_out));
  _2_Input_Mux u_2_input_mux_55 (
    .A(n2_input_mux_39_output), .B(n2_input_mux_47_output), .Output(Output[9]),
    .Sel(n2_input_mux_54_sel_out), .Sel_out(n2_input_mux_55_sel_out));
  _2_Input_Mux u_2_input_mux_56 (
    .A(n2_input_mux_40_output), .B(n2_input_mux_48_output), .Output(Output[8]),
    .Sel(n2_input_mux_55_sel_out), .Sel_out(n2_input_mux_56_sel_out));
  _2_Input_Mux u_2_input_mux_57 (
    .A(n2_input_mux_41_output), .B(n2_input_mux_33_output), .Output(Output[7]),
    .Sel(n2_input_mux_56_sel_out), .Sel_out(n2_input_mux_57_sel_out));
  _2_Input_Mux u_2_input_mux_58 (
    .A(n2_input_mux_42_output), .B(n2_input_mux_34_output), .Output(Output[6]),
    .Sel(n2_input_mux_57_sel_out), .Sel_out(n2_input_mux_58_sel_out));
  _2_Input_Mux u_2_input_mux_59 (
    .A(n2_input_mux_43_output), .B(n2_input_mux_35_output), .Output(Output[5]),
    .Sel(n2_input_mux_58_sel_out), .Sel_out(n2_input_mux_59_sel_out));
  _2_Input_Mux u_2_input_mux_60 (
    .A(n2_input_mux_44_output), .B(n2_input_mux_36_output), .Output(Output[4]),
    .Sel(n2_input_mux_59_sel_out), .Sel_out(n2_input_mux_60_sel_out));
  _2_Input_Mux u_2_input_mux_61 (
    .A(n2_input_mux_45_output), .B(n2_input_mux_37_output), .Output(Output[3]),
    .Sel(n2_input_mux_60_sel_out), .Sel_out(n2_input_mux_61_sel_out));
  _2_Input_Mux u_2_input_mux_62 (
    .A(n2_input_mux_46_output), .B(n2_input_mux_38_output), .Output(Output[2]),
    .Sel(n2_input_mux_61_sel_out), .Sel_out(n2_input_mux_62_sel_out));
  _2_Input_Mux u_2_input_mux_63 (
    .A(n2_input_mux_47_output), .B(n2_input_mux_39_output), .Output(Output[1]),
    .Sel(n2_input_mux_62_sel_out), .Sel_out(n2_input_mux_63_sel_out));
  _2_Input_Mux u_2_input_mux_64 (
    .A(n2_input_mux_48_output), .B(n2_input_mux_40_output), .Output(Output[0]), .Sel(n2_input_mux_63_sel_out));  // open: Sel_out
endmodule

module _16_bit_shifter_side_select__bundled_i_o (
  input  [15:0] Input,
  input  [15:0] Input_2,
  output [15:0] Output
);

  _16_bit_shifter__bundled_i_o u_16_bit_shifter_bundled_i_o_1 (.Input(Input_2), .Output(Output), .in_1(Input[3:0]));
endmodule

module _16_BIT_ALU (
  input  [1:0] Operation,
  input  Invert_A,
  input  Invert_B,
  input  [15:0] A,
  input  [15:0] B,
  output [15:0] Result,
  output CarryOut_Overflow
);

  wire undriven;
  wire [15:0] n16_bit_adder_bundled_i_o_1_out, n16_bit_and_bundled_i_o_1_out,
       n16_bit_inverter_bundled_i_o_1_output, n16_bit_inverter_bundled_i_o_2_output,
       n16_bit_or_bundled_i_o_1_out, n16_bit_shifter_side_select_bundled_i_o_1_output;

  _16_bit_inverter__bundled_i_o u_16_bit_inverter_bundled_i_o_1 (
    .Input(A), .Output(n16_bit_inverter_bundled_i_o_1_output), .Invert_in(Invert_A));
  _16_bit_inverter__bundled_i_o u_16_bit_inverter_bundled_i_o_2 (
    .Input(B), .Output(n16_bit_inverter_bundled_i_o_2_output), .Invert_in(Invert_B));
  _16_bit_shifter_side_select__bundled_i_o u_16_bit_shifter_side_select_bundled_i_o_1 (
    .Input(n16_bit_inverter_bundled_i_o_2_output), .Input_2(n16_bit_inverter_bundled_i_o_1_output),
    .Output(n16_bit_shifter_side_select_bundled_i_o_1_output));
  _16_bit_or__bundled_i_o u_16_bit_or_bundled_i_o_1 (
    .A(n16_bit_inverter_bundled_i_o_1_output), .B(n16_bit_inverter_bundled_i_o_2_output),
    .Out(n16_bit_or_bundled_i_o_1_out));
  _16_bit_and__bundled_i_o u_16_bit_and_bundled_i_o_1 (
    .A(n16_bit_inverter_bundled_i_o_1_output), .B(n16_bit_inverter_bundled_i_o_2_output),
    .Out(n16_bit_and_bundled_i_o_1_out));
  _16_bit_adder__bundled_i_o u_16_bit_adder_bundled_i_o_1 (
    .CarryIn(undriven), .CarryOut(CarryOut_Overflow), .A(n16_bit_inverter_bundled_i_o_1_output),
    .B(n16_bit_inverter_bundled_i_o_2_output), .Out(n16_bit_adder_bundled_i_o_1_out));
  _64_16_MUX__bundled_i_o u_64_16_mux_bundled_i_o_1 (
    .A(n16_bit_shifter_side_select_bundled_i_o_1_output), .B(n16_bit_or_bundled_i_o_1_out),
    .C(n16_bit_and_bundled_i_o_1_out), .D(n16_bit_adder_bundled_i_o_1_out), .Output(Result),
    .Select(Operation));  // open: out_7
endmodule

module _16_bit_alu_2 (
  input  [3:0] in_1,
  input  [15:0] A,
  input  [15:0] B,
  output [15:0] Result,
  output CarryOut_Overflow,
  output [2:0] out_6
);

  wire [15:0] n16_bit_adder_bundled_i_o_1_out, n16_bit_and_bundled_i_o_1_out,
       n16_bit_inverter_bundled_i_o_1_output, n16_bit_inverter_bundled_i_o_2_output,
       n16_bit_or_bundled_i_o_1_out, n16_bit_shifter_side_select_bundled_i_o_1_output;

  _16_bit_inverter__bundled_i_o u_16_bit_inverter_bundled_i_o_1 (
    .Input(A), .Output(n16_bit_inverter_bundled_i_o_1_output), .Invert_in(in_1[3]));
  _16_bit_inverter__bundled_i_o u_16_bit_inverter_bundled_i_o_2 (
    .Input(B), .Output(n16_bit_inverter_bundled_i_o_2_output), .Invert_in(in_1[2]));
  _16_bit_shifter_side_select__bundled_i_o u_16_bit_shifter_side_select_bundled_i_o_1 (
    .Input(n16_bit_inverter_bundled_i_o_2_output), .Input_2(n16_bit_inverter_bundled_i_o_1_output),
    .Output(n16_bit_shifter_side_select_bundled_i_o_1_output));
  _16_bit_or__bundled_i_o u_16_bit_or_bundled_i_o_1 (
    .A(n16_bit_inverter_bundled_i_o_1_output), .B(n16_bit_inverter_bundled_i_o_2_output),
    .Out(n16_bit_or_bundled_i_o_1_out));
  _16_bit_and__bundled_i_o u_16_bit_and_bundled_i_o_1 (
    .A(n16_bit_inverter_bundled_i_o_1_output), .B(n16_bit_inverter_bundled_i_o_2_output),
    .Out(n16_bit_and_bundled_i_o_1_out));
  _16_bit_adder__bundled_i_o u_16_bit_adder_bundled_i_o_1 (
    .CarryIn(in_1[2]), .CarryOut(CarryOut_Overflow), .A(n16_bit_inverter_bundled_i_o_1_output),
    .B(n16_bit_inverter_bundled_i_o_2_output), .Out(n16_bit_adder_bundled_i_o_1_out));
  _64_16_MUX__bundled_i_o u_64_16_mux_bundled_i_o_1 (
    .A(n16_bit_shifter_side_select_bundled_i_o_1_output), .B(n16_bit_or_bundled_i_o_1_out),
    .C(n16_bit_and_bundled_i_o_1_out), .D(n16_bit_adder_bundled_i_o_1_out), .Output(Result),
    .Select(in_1[1:0]));  // open: out_7
  Comparator_part #(.width(16)) comparator_1 (.a(Result), .b({16{1'b0}}), .gt(out_6[0]), .eq(out_6[1]), .lt(out_6[2]));

  // Notes on the sheet:
  //   B: pull=down
endmodule

module Comparator (
  input  [15:0] in_1,
  output NEG,
  output ZERO,
  output POS
);

  // OR_Gate or_1 has open pins: in0=in_1[15:8], in1=in_1[7:0], out=open
  nand nand_1 (ZERO, in_1[15], POS);
  // Probe on ZERO

  assign NEG = in_1[15];

  // Notes on the sheet:
  //   POS: pull=down
  //   NEG: pull=down
  //   ZERO: pull=down
endmodule
